// Logisim project ULA.circ as structural Verilog: 1 circuit, main circuit main
module main (
  input  A7,
  input  A6,
  input  A5,
  input  A4,
  input  A3,
  input  A2,
  input  A1,
  input  A0,
  input  B7,
  input  B6,
  input  B5,
  input  B4,
  input  B3,
  input  B2,
  input  B1,
  input  B0,
  input  in_17,
  input  in_18,
  input  in_19,
  output R7,
  output R6,
  output R5,
  output R4,
  output R3,
  output R2,
  output R1,
  output R0,
  output out_28
);

  wire minus_OVERFLOW, nOVERFLOW, OVERFLOW, plus_OVERFLOW;
  wire [7:0] A, B, demultiplexer_1_out3, demultiplexer_1_out4, demultiplexer_2_out3, demultiplexer_2_out4,
       minus_A, minus_B, minus_R, nA, nB, nR, plus_A, plus_B, plus_R, R, R_t;

  soma Soma (
    .X(plus_A[7]), .Y(plus_B[7]), .in_2(plus_A[6]), .in_10(plus_B[6]), .in_3(plus_A[5]), .in_11(plus_B[5]),
    .in_4(plus_A[4]), .in_12(plus_B[4]), .in_5(plus_A[3]), .in_13(plus_B[3]), .in_6(plus_A[2]),
    .in_14(plus_B[2]), .in_7(plus_A[1]), .in_15(plus_B[1]), .in_8(plus_A[0]), .in_16(plus_B[0]),
    .Z(plus_R[7]), .out_18(plus_R[6]), .out_19(plus_R[5]), .out_20(plus_R[4]), .out_21(plus_R[3]),
    .out_22(plus_R[2]), .out_23(plus_R[1]), .out_24(plus_R[0]), .Overflow(plus_OVERFLOW));
  subtracao_main \Subtração  (
    .x(minus_A[7]), .y(minus_B[7]), .out(minus_R[7]), .in_2(minus_A[6]), .in_10(minus_B[6]),
    .out_19(minus_R[6]), .in_3(minus_A[5]), .in_11(minus_B[5]), .out_20(minus_R[5]), .in_4(minus_A[4]),
    .in_12(minus_B[4]), .out_21(minus_R[4]), .in_5(minus_A[3]), .in_13(minus_B[3]), .out_22(minus_R[3]),
    .in_6(minus_A[2]), .in_14(minus_B[2]), .out_23(minus_R[2]), .in_7(minus_A[1]), .in_15(minus_B[1]),
    .out_24(minus_R[1]), .in_8(minus_A[0]), .in_16(minus_B[0]), .out_25(minus_R[0]), .Overflow(minus_OVERFLOW));
  Demultiplexer #(.select(3), .width(8), .enable("false")) demultiplexer_1 (
    .out0(plus_A), .out1(minus_A), .out2(A), .out3(demultiplexer_1_out3), .out4(demultiplexer_1_out4),
    .in({A0, A1, A2, A3, A4, A5, A6, A7}), .sel({in_17, in_18, in_19}));  // open: out5, out6, out7
  Demultiplexer #(.select(3), .width(8), .enable("false")) demultiplexer_2 (
    .out0(plus_B), .out1(minus_B), .out2(B), .out3(demultiplexer_2_out3), .out4(demultiplexer_2_out4),
    .in({B0, B1, B2, B3, B4, B5, B6, B7}), .sel({in_17, in_18, in_19}));  // open: out5, out6, out7
  assign nA = demultiplexer_1_out3 | demultiplexer_1_out4;  // OR_Gate or_1, 8 bits wide
  assign nB = demultiplexer_2_out3 | demultiplexer_2_out4;  // OR_Gate or_2, 8 bits wide
  divisao_main main_1 (
    .in_9(nA[7]), .in_10(nA[6]), .in_11(nA[5]), .in_12(nA[4]), .in_13(nA[3]), .in_14(nA[2]), .in_15(nA[1]),
    .in_16(nA[0]), .in_1(nB[7]), .in_2(nB[6]), .in_3(nB[5]), .in_4(nB[4]), .in_5(nB[3]), .in_6(nB[2]),
    .in_7(nB[1]), .in_8(nB[0]), .out_18(nR[7]), .out_19(nR[6]), .out_20(nR[5]), .out_21(nR[4]),
    .out_22(nR[3]), .out_23(nR[2]), .out_24(nR[1]), .out_25(nR[0]), .out_26(R[7]), .out_27(R[6]),
    .out_28(R[5]), .out_29(R[4]), .out_30(R[3]), .out_31(R[2]), .out_32(R[1]), .out_33(R[0]),
    .out_17(nOVERFLOW));
  Multiplexer #(.select(3), .width(8), .enable("false")) multiplexer_1 (
    .in0(plus_R), .in1(minus_R), .in2(R_t), .in3(nR), .in4(R), .out({R0, R1, R2, R3, R4, R5, R6, R7}),
    .sel({in_17, in_18, in_19}));  // open: in5, in6, in7
  or or_3 (out_28, plus_OVERFLOW, minus_OVERFLOW, OVERFLOW, nOVERFLOW);
  // multiplicacao_main Multiplicação: pin names not known; wires that end beside it: A[7], R_t[7], A[6], R_t[6], A[5], R_t[5], A[4], R_t[4], A[3], R_t[3], A[2], R_t[2], A[1], R_t[1], A[0], R_t[0], B[7], B[6], B[5], B[4], B[3], B[2], B[1], B[0], OVERFLOW

  // Other names for the same wires on the sheet: A_t[7:0] = {A0, A1, A2, A3, A4, A5, A6, A7};
  //   B_t[7:0] = {B0, B1, B2, B3, B4, B5, B6, B7}; OVERFLOW_t = out_28; R_t_t[7:0] = {R0, R1, R2, R3, R4, R5, R6, R7};
  //   SEL[2:0] = {in_17, in_18, in_19}
endmodule
