// Logisim project subtracVfinale2.circ as structural Verilog: 1 circuit, main circuit main
module main (
  input  x,
  input  in_2,
  input  in_3,
  input  in_4,
  input  in_5,
  input  in_6,
  input  in_7,
  input  in_8,
  input  y,
  input  in_10,
  input  in_11,
  input  in_12,
  input  in_13,
  input  in_14,
  input  in_15,
  input  in_16,
  output Overflow,
  output out,
  output out_19,
  output out_20,
  output out_21,
  output out_22,
  output out_23,
  output out_24,
  output out_25
);

  wire and_1_out, and_2_out, and_3_out, and_4_out, and_5_out, and_6_out, and_7_out, and_8_out, and_9_out,
       and_10_out, and_11_out, and_12_out, and_13_out, and_14_out, and_15_out, not_1_out, not_2_out,
       not_3_out, not_4_out, not_5_out, not_6_out, not_7_out, not_8_out, not_9_out, not_10_out, not_11_out,
       not_12_out, not_13_out, not_14_out, not_15_out, not_16_out, or_1_out, or_2_out, or_3_out, or_4_out,
       or_5_out, or_6_out, xor_2_out, xor_4_out, xor_6_out, xor_9_out, xor_11_out, xor_12_out, xor_14_out;

  xor xor_1 (out, x, y);
  not not_1 (not_1_out, x);
  and and_1 (and_1_out, not_1_out, y);
  xor xor_2 (xor_2_out, in_2, in_10);
  xor xor_3 (out_19, and_1_out, xor_2_out);
  not not_2 (not_2_out, in_2);
  and and_2 (and_2_out, not_2_out, in_10);
  and and_3 (and_3_out, and_1_out, not_3_out);
  not not_3 (not_3_out, xor_2_out);
  or or_1 (or_1_out, and_2_out, and_3_out);
  xor xor_4 (xor_4_out, in_3, in_11);
  xor xor_5 (out_20, or_1_out, xor_4_out);
  not not_4 (not_4_out, in_3);
  not not_5 (not_5_out, xor_4_out);
  and and_4 (and_4_out, not_4_out, in_11);
  and and_5 (and_5_out, or_1_out, not_5_out);
  xor xor_6 (xor_6_out, in_4, in_12);
  or or_2 (or_2_out, and_4_out, and_5_out);
  xor xor_7 (out_21, or_2_out, xor_6_out);
  not not_6 (not_6_out, in_4);
  not not_7 (not_7_out, xor_6_out);
  and and_6 (and_6_out, not_6_out, in_12);
  and and_7 (and_7_out, or_2_out, not_7_out);
  or or_3 (or_3_out, and_6_out, and_7_out);
  xor xor_8 (out_22, or_3_out, xor_9_out);
  not not_8 (not_8_out, in_5);
  xor xor_9 (xor_9_out, in_5, in_13);
  not not_9 (not_9_out, xor_9_out);
  and and_8 (and_8_out, not_8_out, in_13);
  and and_9 (and_9_out, or_3_out, not_9_out);
  or or_4 (or_4_out, and_8_out, and_9_out);
  xor xor_10 (out_23, or_4_out, xor_11_out);
  not not_10 (not_10_out, in_6);
  xor xor_11 (xor_11_out, in_6, in_14);
  not not_11 (not_11_out, xor_11_out);
  and and_10 (and_10_out, not_10_out, in_14);
  and and_11 (and_11_out, or_4_out, not_11_out);
  or or_5 (or_5_out, and_10_out, and_11_out);
  not not_12 (not_12_out, in_7);
  xor xor_12 (xor_12_out, in_7, in_15);
  not not_13 (not_13_out, xor_12_out);
  xor xor_13 (out_24, or_5_out, xor_12_out);
  and and_12 (and_12_out, not_12_out, in_15);
  and and_13 (and_13_out, or_5_out, not_13_out);
  or or_6 (or_6_out, and_12_out, and_13_out);
  xor xor_14 (xor_14_out, in_8, in_16);
  xor xor_15 (out_25, or_6_out, xor_14_out);
  not not_14 (not_14_out, in_16);
  not not_15 (not_15_out, out_25);
  not not_16 (not_16_out, in_8);
  and and_14 (and_14_out, in_8, not_14_out, not_15_out);
  and and_15 (and_15_out, not_16_out, in_16, out_25, out_25);
  or or_7 (Overflow, and_14_out, and_15_out);
endmodule
