// Logisim project inversor.circ as structural Verilog: 1 circuit, main circuit main
module main (
  input  in_1,
  input  in_2,
  input  in_3,
  input  in_4,
  input  in_5,
  input  in_6,
  input  in_7,
  input  in_8,
  input  in_9,
  output out_10,
  output out_11,
  output out_12,
  output out_13,
  output out_14,
  output out_15,
  output out_16,
  output out_17
);

  wire and_1_out, and_2_out, and_3_out, and_4_out, and_5_out, and_6_out, and_7_out, and_8_out, and_9_out,
       and_10_out, and_11_out, and_12_out, and_13_out, and_14_out, and_15_out, and_16_out, not_1_out,
       not_2_out, not_3_out, not_4_out, not_5_out, not_6_out, not_7_out, not_8_out, not_9_out, S0, S1, S2,
       S3, S4, S5, S6, S7;

  not not_1 (not_1_out, in_1);
  soma soma_1 (
    .X(not_1_out), .Y(1'b1), .in_2(not_4_out), .in_10(1'b0), .in_3(not_5_out), .in_11(1'b0),
    .in_4(not_3_out), .in_12(1'b0), .in_5(not_6_out), .in_13(1'b0), .in_6(not_7_out), .in_14(1'b0),
    .in_7(not_8_out), .in_15(1'b0), .in_8(not_9_out), .in_16(1'b0), .Z(S0), .out_18(S1), .out_19(S2),
    .out_20(S3), .out_21(S4), .out_22(S5), .out_23(S6), .out_24(S7));  // open: Overflow
  not not_2 (not_2_out, in_9);
  and and_1 (and_1_out, not_2_out, in_1);
  or or_1 (out_10, and_1_out, and_2_out);
  not not_3 (not_3_out, in_4);
  not not_4 (not_4_out, in_2);
  not not_5 (not_5_out, in_3);
  not not_6 (not_6_out, in_5);
  and and_2 (and_2_out, in_9, S0);
  and and_3 (and_3_out, not_2_out, in_2);
  not not_7 (not_7_out, in_6);
  not not_8 (not_8_out, in_7);
  not not_9 (not_9_out, in_8);
  and and_4 (and_4_out, in_9, S1);
  or or_2 (out_11, and_3_out, and_4_out);
  and and_5 (and_5_out, in_9, S2);
  and and_6 (and_6_out, not_2_out, in_3);
  or or_3 (out_12, and_6_out, and_5_out);
  and and_7 (and_7_out, in_9, S3);
  and and_8 (and_8_out, not_2_out, in_4);
  or or_4 (out_13, and_8_out, and_7_out);
  and and_9 (and_9_out, not_2_out, in_5);
  and and_10 (and_10_out, in_9, S4);
  or or_5 (out_14, and_9_out, and_10_out);
  and and_11 (and_11_out, not_2_out, in_6);
  and and_12 (and_12_out, in_9, S5);
  or or_6 (out_15, and_11_out, and_12_out);
  and and_13 (and_13_out, not_2_out, in_7);
  and and_14 (and_14_out, in_9, S6);
  or or_7 (out_16, and_13_out, and_14_out);
  and and_15 (and_15_out, not_2_out, in_8);
  or or_8 (out_17, and_15_out, and_16_out);
  and and_16 (and_16_out, in_9, S7);

  // Other names for the same wires on the sheet: E0 = in_1; E1 = in_2; E2 = in_3; E3 = in_4; E4 = in_5; E5 = in_6;
  //   E6 = in_7; E7 = in_8; Enable = in_9
endmodule
