// Logisim project somaSecondTRy.circ as structural Verilog: 3 circuits, main circuit main
module soma (
  input  carry_in,
  input  X,
  input  in_3,
  input  in_4,
  input  in_5,
  input  in_6,
  input  in_7,
  input  in_8,
  input  in_9,
  input  Y,
  input  in_11,
  input  in_12,
  input  in_13,
  input  in_14,
  input  in_15,
  input  in_16,
  input  in_17,
  output out_18,
  output out_19,
  output out_20,
  output out_21,
  output out_22,
  output out_23,
  output out_24,
  output Z,
  output out_26
);

  wire and_1_out, and_2_out, and_3_out, and_4_out, and_5_out, and_6_out, and_7_out, and_8_out, and_9_out,
       and_10_out, and_11_out, and_12_out, and_13_out, and_14_out, and_15_out, and_16_out, or_1_out,
       or_2_out, or_3_out, or_4_out, or_5_out, or_6_out, or_7_out, xor_1_out, xor_3_out, xor_5_out,
       xor_7_out, xor_9_out, xor_11_out, xor_13_out, xor_15_out;

  xor xor_1 (xor_1_out, X, Y);
  xor xor_2 (Z, xor_1_out, carry_in);
  and and_1 (and_1_out, Y, X);
  or or_1 (or_1_out, and_1_out, and_2_out);
  and and_2 (and_2_out, xor_1_out, carry_in);
  xor xor_3 (xor_3_out, in_3, in_11);
  xor xor_4 (out_18, xor_3_out, or_1_out);
  and and_3 (and_3_out, in_11, in_3);
  and and_4 (and_4_out, or_1_out, xor_3_out);
  or or_2 (or_2_out, and_3_out, and_4_out);
  xor xor_5 (xor_5_out, in_4, in_12);
  xor xor_6 (out_19, xor_5_out, or_2_out);
  and and_5 (and_5_out, in_12, in_4);
  and and_6 (and_6_out, or_2_out, xor_5_out);
  or or_3 (or_3_out, and_5_out, and_6_out);
  xor xor_7 (xor_7_out, in_5, in_13);
  xor xor_8 (out_20, xor_7_out, or_3_out);
  and and_7 (and_7_out, in_13, in_5);
  and and_8 (and_8_out, or_3_out, xor_7_out);
  or or_4 (or_4_out, and_7_out, and_8_out);
  xor xor_9 (xor_9_out, in_6, in_14);
  xor xor_10 (out_21, xor_9_out, or_4_out);
  and and_9 (and_9_out, in_14, in_6);
  and and_10 (and_10_out, or_4_out, xor_9_out);
  or or_5 (or_5_out, and_9_out, and_10_out);
  xor xor_11 (xor_11_out, in_7, in_15);
  xor xor_12 (out_22, xor_11_out, or_5_out);
  and and_11 (and_11_out, in_15, in_7);
  or or_6 (or_6_out, and_11_out, and_12_out);
  and and_12 (and_12_out, or_5_out, xor_11_out);
  xor xor_13 (xor_13_out, in_8, in_16);
  xor xor_14 (out_23, xor_13_out, or_6_out);
  and and_13 (and_13_out, in_16, in_8);
  and and_14 (and_14_out, or_6_out, xor_13_out);
  or or_7 (or_7_out, and_13_out, and_14_out);
  xor xor_15 (xor_15_out, in_9, in_17);
  xor xor_16 (out_24, xor_15_out, or_7_out);
  and and_15 (and_15_out, in_17, in_9);
  and and_16 (and_16_out, or_7_out, xor_15_out);
  or or_8 (out_26, and_15_out, and_16_out);

  // Notes on the sheet:
  //   in_14: pull=down
  //   in_13: pull=down
  //   in_12: pull=down
  //   in_15: pull=down
  //   Y: pull=down
  //   in_16: pull=down
  //   in_17: pull=down
  //   in_11: pull=down
  //   carry out
  //   carry out
  //   carry out
  //   carry out
  //   carry out
  //   carry out
  //   carry out
  //   overflow
  //   carry out
endmodule

module main (
  input  in_1,
  input  in_2,
  input  in_3,
  input  in_4,
  input  in_5,
  input  in_6,
  input  in_7,
  input  in_8,
  input  in_9,
  input  in_10,
  output out_11,
  output out_12
);

  wire auxiliar_1_out_10, auxiliar_1_out_11, auxiliar_1_out_12, auxiliar_1_out_13, auxiliar_1_out_14,
       auxiliar_1_out_15, auxiliar_1_out_16, auxiliar_1_out_17, auxiliar_2_out_10, auxiliar_2_out_11,
       auxiliar_2_out_12, auxiliar_2_out_13, auxiliar_2_out_14, auxiliar_2_out_15, auxiliar_2_out_16,
       auxiliar_2_out_17, auxiliar_3_out_17, soma_1_out_18, soma_1_out_19, soma_1_out_20, soma_1_out_21,
       soma_1_out_22, soma_1_out_23, soma_1_out_24, soma_1_out_26, undriven, undriven_2, undriven_3,
       undriven_4;

  soma soma_1 (
    .X(1'b0), .Y(auxiliar_1_out_10), .in_3(1'b0), .in_11(auxiliar_1_out_11), .in_4(1'b0),
    .in_12(auxiliar_1_out_12), .in_5(1'b0), .in_13(auxiliar_1_out_13), .in_6(1'b0),
    .in_14(auxiliar_1_out_14), .in_7(1'b0), .in_15(auxiliar_1_out_15), .in_8(1'b0),
    .in_16(auxiliar_1_out_16), .in_9(1'b0), .in_17(auxiliar_1_out_17), .Z(out_11), .out_18(soma_1_out_18),
    .out_19(soma_1_out_19), .out_20(soma_1_out_20), .out_21(soma_1_out_21), .out_22(soma_1_out_22),
    .out_23(soma_1_out_23), .out_24(soma_1_out_24), .out_26(soma_1_out_26), .carry_in(1'b0));
  soma soma_2 (
    .X(soma_1_out_18), .Y(auxiliar_2_out_10), .in_3(soma_1_out_19), .in_11(auxiliar_2_out_11),
    .in_4(soma_1_out_20), .in_12(auxiliar_2_out_12), .in_5(soma_1_out_21), .in_13(auxiliar_2_out_13),
    .in_6(soma_1_out_22), .in_14(auxiliar_2_out_14), .in_7(soma_1_out_23), .in_15(auxiliar_2_out_15),
    .in_8(soma_1_out_24), .in_16(auxiliar_2_out_16), .in_9(soma_1_out_26), .in_17(auxiliar_2_out_17),
    .Z(out_12), .carry_in(1'b0));  // open: out_18, out_19, out_20, out_21, out_22, out_23, out_24, out_26
  soma soma_3 (
    .X(undriven), .Y(auxiliar_2_out_11), .in_3(undriven_2), .in_11(auxiliar_2_out_12), .in_4(soma_1_out_21),
    .in_12(auxiliar_2_out_13), .in_5(soma_1_out_22), .in_13(auxiliar_2_out_14), .in_6(soma_1_out_23),
    .in_14(auxiliar_2_out_15), .in_7(soma_1_out_24), .in_15(auxiliar_2_out_16), .in_8(undriven_3),
    .in_16(auxiliar_2_out_17), .in_9(undriven_4), .in_17(auxiliar_3_out_17), .Z(out_12));  // open: out_18, out_19, out_20, out_21, out_22, out_23, out_24, out_26, carry_in
  auxiliar auxiliar_1 (
    .in_9(in_9), .in_1(in_1), .in_2(in_2), .in_3(in_3), .in_4(in_4), .in_5(in_5), .in_6(in_6), .in_7(in_7),
    .in_8(in_8), .out_10(auxiliar_1_out_10), .out_11(auxiliar_1_out_11), .out_12(auxiliar_1_out_12),
    .out_13(auxiliar_1_out_13), .out_14(auxiliar_1_out_14), .out_15(auxiliar_1_out_15),
    .out_16(auxiliar_1_out_16), .out_17(auxiliar_1_out_17));
  auxiliar auxiliar_2 (
    .in_9(in_10), .in_1(in_1), .in_2(in_2), .in_3(in_3), .in_4(in_4), .in_5(in_5), .in_6(in_6), .in_7(in_7),
    .in_8(in_8), .out_10(auxiliar_2_out_10), .out_11(auxiliar_2_out_11), .out_12(auxiliar_2_out_12),
    .out_13(auxiliar_2_out_13), .out_14(auxiliar_2_out_14), .out_15(auxiliar_2_out_15),
    .out_16(auxiliar_2_out_16), .out_17(auxiliar_2_out_17));
  auxiliar auxiliar_3 (
    .in_1(in_1), .in_2(in_2), .in_3(in_3), .in_4(in_4), .in_5(in_5), .in_6(in_6), .in_7(in_7), .in_8(in_8),
    .out_10(auxiliar_2_out_11), .out_11(auxiliar_2_out_12), .out_12(auxiliar_2_out_13),
    .out_13(auxiliar_2_out_14), .out_14(auxiliar_2_out_15), .out_15(auxiliar_2_out_16),
    .out_16(auxiliar_2_out_17), .out_17(auxiliar_3_out_17));  // open: in_9

  // Other names for the same wires on the sheet: _0 = in_1; _1 = in_2; _2 = in_3; _3 = in_4; _4 = in_5; _5 = in_6;
  //   _6 = in_7; _7 = in_8; S0 = out_11; S1 = out_12
endmodule

module auxiliar (
  input  in_1,
  input  in_2,
  input  in_3,
  input  in_4,
  input  in_5,
  input  in_6,
  input  in_7,
  input  in_8,
  input  in_9,
  output out_10,
  output out_11,
  output out_12,
  output out_13,
  output out_14,
  output out_15,
  output out_16,
  output out_17
);

  and and_1 (out_10, in_1, in_9);
  and and_2 (out_11, in_2, in_9);
  and and_3 (out_12, in_3, in_9);
  and and_4 (out_13, in_4, in_9);
  and and_5 (out_14, in_5, in_9);
  and and_6 (out_15, in_6, in_9);
  and and_7 (out_16, in_7, in_9);
  and and_8 (out_17, in_8, in_9);
endmodule
