// Logisim project subParaDiv.circ as structural Verilog: 1 circuit, main circuit main
module main (
  input  in_1,
  input  in_2,
  input  in_3,
  input  in_4,
  input  in_5,
  input  in_6,
  input  in_7,
  input  in_8,
  input  in_9,
  input  in_10,
  input  in_11,
  input  in_12,
  input  in_13,
  input  in_14,
  input  in_15,
  input  in_16,
  output out_17,
  output out_18,
  output out_19,
  output out_20,
  output out_21,
  output out_22,
  output out_23,
  output out_24,
  output out_25
);

  wire and_1_out, and_2_out, and_3_out, and_4_out, and_5_out, and_6_out, and_7_out, and_8_out, and_9_out,
       and_10_out, and_11_out, and_12_out, and_13_out, and_14_out, and_15_out, and_16_out, OVERFLOW, S0, S1,
       S2, S3, S4, S5, S6, S7;

  and and_1 (and_1_out, out_25, S0);
  and and_2 (and_2_out, OVERFLOW, in_1);
  or or_1 (out_17, and_2_out, and_1_out);
  and and_3 (and_3_out, OVERFLOW, in_2);
  and and_4 (and_4_out, out_25, S1);
  or or_2 (out_18, and_3_out, and_4_out);
  subtracVfinale_main main_1 (
    .x(in_1), .y(in_9), .out(S0), .in_2(in_2), .in_10(in_10), .out_19(S1), .in_3(in_3), .in_11(in_11),
    .out_20(S2), .in_4(in_4), .in_12(in_12), .out_21(S3), .in_5(in_5), .in_13(in_13), .out_22(S4),
    .in_6(in_6), .in_14(in_14), .out_23(S5), .in_7(in_7), .in_15(in_15), .out_24(S6), .in_8(in_8),
    .in_16(in_16), .out_25(S7), .overflow(OVERFLOW));
  and and_5 (and_5_out, out_25, S2);
  and and_6 (and_6_out, OVERFLOW, in_3);
  or or_3 (out_19, and_6_out, and_5_out);
  and and_7 (and_7_out, out_25, S3);
  and and_8 (and_8_out, OVERFLOW, in_4);
  or or_4 (out_20, and_8_out, and_7_out);
  not not_1 (out_25, OVERFLOW);
  and and_9 (and_9_out, OVERFLOW, in_5);
  or or_5 (out_21, and_9_out, and_10_out);
  and and_10 (and_10_out, out_25, S4);
  and and_11 (and_11_out, OVERFLOW, in_6);
  or or_6 (out_22, and_11_out, and_12_out);
  and and_12 (and_12_out, out_25, S5);
  and and_13 (and_13_out, OVERFLOW, in_7);
  and and_14 (and_14_out, out_25, S6);
  and and_15 (and_15_out, OVERFLOW, in_8);
  or or_7 (out_23, and_13_out, and_14_out);
  and and_16 (and_16_out, out_25, S7);
  or or_8 (out_24, and_15_out, and_16_out);

  // Other names for the same wires on the sheet: A0 = in_1; A1 = in_2; A2 = in_3; A3 = in_4; A4 = in_5; A5 = in_6;
  //   A6 = in_7; A7 = in_8; B0 = in_9; B1 = in_10; B2 = in_11; B3 = in_12; B4 = in_13; B5 = in_14; B6 = in_15;
  //   B7 = in_16; OVERFLOW_t = out_25
endmodule
