// Logisim project divisao.circ as structural Verilog: 4 circuits, main circuit main
module main (
  input  in_1,
  input  in_2,
  input  in_3,
  input  in_4,
  input  in_5,
  input  in_6,
  input  in_7,
  input  in_8,
  input  in_9,
  input  in_10,
  input  in_11,
  input  in_12,
  input  in_13,
  input  in_14,
  input  in_15,
  input  in_16,
  output out_17,
  output out_18,
  output out_19,
  output out_20,
  output out_21,
  output out_22,
  output out_23,
  output out_24,
  output out_25,
  output out_26,
  output out_27,
  output out_28,
  output out_29,
  output out_30,
  output out_31,
  output out_32
);

  wire A0, A1, A2, A3, A4, A5, A6, A7, auxiliar_1_out_18, auxiliar_1_out_19, auxiliar_2_out_18,
       auxiliar_2_out_19, auxiliar_2_out_20, auxiliar_3_out_18, auxiliar_3_out_19, auxiliar_3_out_20,
       auxiliar_3_out_21, auxiliar_4_out_18, auxiliar_4_out_19, auxiliar_4_out_20, auxiliar_4_out_21,
       auxiliar_4_out_22, auxiliar_5_out_18, auxiliar_5_out_19, auxiliar_5_out_20, auxiliar_5_out_21,
       auxiliar_5_out_22, auxiliar_5_out_23, auxiliar_6_out_18, auxiliar_6_out_19, auxiliar_6_out_20,
       auxiliar_6_out_21, auxiliar_6_out_22, auxiliar_6_out_23, auxiliar_6_out_24, auxiliar_7_out_18,
       auxiliar_7_out_19, auxiliar_7_out_20, auxiliar_7_out_21, auxiliar_7_out_22, auxiliar_7_out_23,
       auxiliar_7_out_24, auxiliar_7_out_25, auxiliar_8_out_18, B0, B1, B2, B3, B4, B5, B6, B7, Q0, Q1, Q2,
       Q3, Q4, Q5, Q6, Q7, R0, R1, R2, R3, R4, R5, R6, R7, xor_1_out;

  auxiliar auxiliar_1 (
    .in_1(A7), .in_2(1'b0), .in_3(1'b0), .in_4(1'b0), .in_5(1'b0), .in_6(1'b0), .in_7(1'b0), .in_8(1'b0),
    .in_9(B0), .in_10(B1), .in_11(B2), .in_12(B3), .in_13(B4), .in_14(B5), .in_15(B6), .in_16(B7),
    .out_19(auxiliar_1_out_19), .out_18(auxiliar_1_out_18), .in_17(1'b1));  // open: out_20, out_21, out_22, out_23, out_24, out_25, out_26
  auxiliar auxiliar_2 (
    .in_1(A6), .in_2(auxiliar_1_out_19), .in_3(1'b0), .in_4(1'b0), .in_5(1'b0), .in_6(1'b0), .in_7(1'b0),
    .in_8(1'b0), .in_9(B0), .in_10(B1), .in_11(B2), .in_12(B3), .in_13(B4), .in_14(B5), .in_15(B6),
    .in_16(B7), .out_19(auxiliar_2_out_19), .out_20(auxiliar_2_out_20), .out_18(auxiliar_2_out_18),
    .in_17(1'b1));  // open: out_21, out_22, out_23, out_24, out_25, out_26
  auxiliar auxiliar_3 (
    .in_1(A5), .in_2(auxiliar_2_out_19), .in_3(auxiliar_2_out_20), .in_4(1'b0), .in_5(1'b0), .in_6(1'b0),
    .in_7(1'b0), .in_8(1'b0), .in_9(B0), .in_10(B1), .in_11(B2), .in_12(B3), .in_13(B4), .in_14(B5),
    .in_15(B6), .in_16(B7), .out_19(auxiliar_3_out_19), .out_20(auxiliar_3_out_20),
    .out_21(auxiliar_3_out_21), .out_18(auxiliar_3_out_18), .in_17(1'b1));  // open: out_22, out_23, out_24, out_25, out_26
  auxiliar auxiliar_4 (
    .in_1(A4), .in_2(auxiliar_3_out_19), .in_3(auxiliar_3_out_20), .in_4(auxiliar_3_out_21), .in_5(1'b0),
    .in_6(1'b0), .in_7(1'b0), .in_8(1'b0), .in_9(B0), .in_10(B1), .in_11(B2), .in_12(B3), .in_13(B4),
    .in_14(B5), .in_15(B6), .in_16(B7), .out_19(auxiliar_4_out_19), .out_20(auxiliar_4_out_20),
    .out_21(auxiliar_4_out_21), .out_22(auxiliar_4_out_22), .out_18(auxiliar_4_out_18), .in_17(1'b1));  // open: out_23, out_24, out_25, out_26
  auxiliar auxiliar_5 (
    .in_1(A3), .in_2(auxiliar_4_out_19), .in_3(auxiliar_4_out_20), .in_4(auxiliar_4_out_21),
    .in_5(auxiliar_4_out_22), .in_6(1'b0), .in_7(1'b0), .in_8(1'b0), .in_9(B0), .in_10(B1), .in_11(B2),
    .in_12(B3), .in_13(B4), .in_14(B5), .in_15(B6), .in_16(B7), .out_19(auxiliar_5_out_19),
    .out_20(auxiliar_5_out_20), .out_21(auxiliar_5_out_21), .out_22(auxiliar_5_out_22),
    .out_23(auxiliar_5_out_23), .out_18(auxiliar_5_out_18), .in_17(1'b1));  // open: out_24, out_25, out_26
  auxiliar auxiliar_6 (
    .in_1(A2), .in_2(auxiliar_5_out_19), .in_3(auxiliar_5_out_20), .in_4(auxiliar_5_out_21),
    .in_5(auxiliar_5_out_22), .in_6(auxiliar_5_out_23), .in_7(1'b0), .in_8(1'b0), .in_9(B0), .in_10(B1),
    .in_11(B2), .in_12(B3), .in_13(B4), .in_14(B5), .in_15(B6), .in_16(B7), .out_19(auxiliar_6_out_19),
    .out_20(auxiliar_6_out_20), .out_21(auxiliar_6_out_21), .out_22(auxiliar_6_out_22),
    .out_23(auxiliar_6_out_23), .out_24(auxiliar_6_out_24), .out_18(auxiliar_6_out_18), .in_17(1'b1));  // open: out_25, out_26
  auxiliar auxiliar_7 (
    .in_1(A1), .in_2(auxiliar_6_out_19), .in_3(auxiliar_6_out_20), .in_4(auxiliar_6_out_21),
    .in_5(auxiliar_6_out_22), .in_6(auxiliar_6_out_23), .in_7(auxiliar_6_out_24), .in_8(1'b0), .in_9(B0),
    .in_10(B1), .in_11(B2), .in_12(B3), .in_13(B4), .in_14(B5), .in_15(B6), .in_16(B7),
    .out_19(auxiliar_7_out_19), .out_20(auxiliar_7_out_20), .out_21(auxiliar_7_out_21),
    .out_22(auxiliar_7_out_22), .out_23(auxiliar_7_out_23), .out_24(auxiliar_7_out_24),
    .out_25(auxiliar_7_out_25), .out_18(auxiliar_7_out_18), .in_17(1'b1));  // open: out_26
  auxiliar auxiliar_8 (
    .in_1(A0), .in_2(auxiliar_7_out_19), .in_3(auxiliar_7_out_20), .in_4(auxiliar_7_out_21),
    .in_5(auxiliar_7_out_22), .in_6(auxiliar_7_out_23), .in_7(auxiliar_7_out_24), .in_8(auxiliar_7_out_25),
    .in_9(B0), .in_10(B1), .in_11(B2), .in_12(B3), .in_13(B4), .in_14(B5), .in_15(B6), .in_16(B7),
    .out_19(R0), .out_20(R1), .out_21(R2), .out_22(R3), .out_23(R4), .out_24(R5), .out_25(R6), .out_26(R7),
    .out_18(auxiliar_8_out_18), .in_17(1'b1));
  inversor_main main_1 (
    .in_1(in_9), .in_2(in_10), .in_3(in_11), .in_4(in_12), .in_5(in_13), .in_6(in_14), .in_7(in_15),
    .in_8(in_16), .in_9(in_16), .out_10(A0), .out_11(A1), .out_12(A2), .out_13(A3), .out_14(A4), .out_15(A5),
    .out_16(A6), .out_17(A7));
  xor xor_1 (xor_1_out, in_8, in_16);
  inversor_main main_2 (
    .in_1(Q0), .in_2(Q1), .in_3(Q2), .in_4(Q3), .in_5(Q4), .in_6(Q5), .in_7(Q6), .in_8(Q7), .in_9(xor_1_out),
    .out_10(out_17), .out_11(out_18), .out_12(out_19), .out_13(out_20), .out_14(out_21), .out_15(out_22),
    .out_16(out_23), .out_17(out_24));
  not not_1 (Q7, auxiliar_1_out_18);
  not not_2 (Q6, auxiliar_2_out_18);
  not not_3 (Q5, auxiliar_3_out_18);
  not not_4 (Q4, auxiliar_4_out_18);
  not not_5 (Q3, auxiliar_5_out_18);
  not not_6 (Q2, auxiliar_6_out_18);
  not not_7 (Q1, auxiliar_7_out_18);
  not not_8 (Q0, auxiliar_8_out_18);
  inversor_main main_3 (
    .in_1(in_1), .in_2(in_2), .in_3(in_3), .in_4(in_4), .in_5(in_5), .in_6(in_6), .in_7(in_7), .in_8(in_8),
    .in_9(in_8), .out_10(B0), .out_11(B1), .out_12(B2), .out_13(B3), .out_14(B4), .out_15(B5), .out_16(B6),
    .out_17(B7));
  Resto_negativo resto_negativo_1 (
    .in_17(in_16), .in_1(B0), .in_2(B1), .in_3(B2), .in_4(B3), .in_5(B4), .in_6(B5), .in_7(B6), .in_8(B7),
    .in_9(R0), .in_10(R1), .in_11(R2), .in_12(R3), .in_13(R4), .in_14(R5), .in_15(R6), .in_16(R7),
    .out_18(out_25), .out_19(out_26), .out_20(out_27), .out_21(out_28), .out_22(out_29), .out_23(out_30),
    .out_24(out_31), .out_25(out_32));

  // Other names for the same wires on the sheet: D0 = in_1; D1 = in_2; D2 = in_3; D3 = in_4; D4 = in_5; D5 = in_6;
  //   D6 = in_7; D7 = in_8
endmodule

module auxiliar (
  input  in_1,
  input  in_2,
  input  in_3,
  input  in_4,
  input  in_5,
  input  in_6,
  input  in_7,
  input  in_8,
  input  in_9,
  input  in_10,
  input  in_11,
  input  in_12,
  input  in_13,
  input  in_14,
  input  in_15,
  input  in_16,
  input  in_17,
  output out_18,
  output out_19,
  output out_20,
  output out_21,
  output out_22,
  output out_23,
  output out_24,
  output out_25,
  output out_26
);

  wire and_1_out, and_2_out, and_3_out, and_4_out, and_5_out, and_6_out, and_7_out, and_8_out, and_9_out,
       and_10_out, and_11_out, and_12_out, and_13_out, and_14_out, and_15_out, and_16_out, not_1_out, S0, S1,
       S2, S3, S4, S5, S6, S7;

  not not_1 (not_1_out, out_18);
  and and_1 (and_1_out, out_18, in_1);
  and and_2 (and_2_out, not_1_out, S0);
  or or_1 (out_19, and_1_out, and_2_out);
  and and_3 (and_3_out, not_1_out, S1);
  and and_4 (and_4_out, out_18, in_2);
  or or_2 (out_20, and_4_out, and_3_out);
  and and_5 (and_5_out, not_1_out, S2);
  and and_6 (and_6_out, out_18, in_3);
  or or_3 (out_21, and_6_out, and_5_out);
  and and_7 (and_7_out, out_18, in_4);
  and and_8 (and_8_out, not_1_out, S3);
  or or_4 (out_22, and_7_out, and_8_out);
  subtracao_parcial subtracao_parcial_1 (
    .x(in_1), .in_2(in_2), .in_3(in_3), .in_4(in_4), .in_5(in_5), .in_6(in_6), .in_7(in_7), .in_8(in_8),
    .y(in_9), .in_10(in_10), .in_11(in_11), .in_12(in_12), .in_13(in_13), .in_14(in_14), .in_15(in_15),
    .in_16(in_16), .overflow(out_18), .out(S0), .out_19(S1), .out_20(S2), .out_21(S3), .out_22(S4),
    .out_23(S5), .out_24(S6), .out_25(S7));
  and and_9 (and_9_out, out_18, in_5);
  or or_5 (out_23, and_9_out, and_10_out);
  and and_10 (and_10_out, not_1_out, S4);
  and and_11 (and_11_out, out_18, in_6);
  or or_6 (out_24, and_11_out, and_12_out);
  and and_12 (and_12_out, not_1_out, S5);
  and and_13 (and_13_out, out_18, in_7);
  and and_14 (and_14_out, not_1_out, S6);
  and and_15 (and_15_out, out_18, in_8);
  or or_7 (out_25, and_13_out, and_14_out);
  and and_16 (and_16_out, not_1_out, S7);
  or or_8 (out_26, and_15_out, and_16_out);

  // Other names for the same wires on the sheet: A0 = in_1; A1 = in_2; A2 = in_3; A3 = in_4; A4 = in_5; A5 = in_6;
  //   A6 = in_7; A7 = in_8; B0 = in_9; B1 = in_10; B2 = in_11; B3 = in_12; B4 = in_13; B5 = in_14; B6 = in_15;
  //   B7 = in_16; Enable = in_17; overflow = out_18
endmodule

module subtracao_parcial (
  input  x,
  input  in_2,
  input  in_3,
  input  in_4,
  input  in_5,
  input  in_6,
  input  in_7,
  input  in_8,
  input  y,
  input  in_10,
  input  in_11,
  input  in_12,
  input  in_13,
  input  in_14,
  input  in_15,
  input  in_16,
  output overflow,
  output out,
  output out_19,
  output out_20,
  output out_21,
  output out_22,
  output out_23,
  output out_24,
  output out_25
);

  wire and_1_out, and_2_out, and_3_out, and_4_out, and_5_out, and_6_out, and_7_out, and_8_out, and_9_out,
       and_10_out, and_11_out, and_12_out, and_13_out, and_14_out, and_15_out, not_1_out, not_2_out,
       not_3_out, not_4_out, not_5_out, not_6_out, not_7_out, not_8_out, not_9_out, not_10_out, not_11_out,
       not_12_out, not_13_out, not_14_out, not_15_out, or_1_out, or_2_out, or_3_out, or_4_out, or_5_out,
       or_6_out, xor_2_out, xor_4_out, xor_6_out, xor_9_out, xor_11_out, xor_12_out, xor_14_out;

  xor xor_1 (out, x, y);
  not not_1 (not_1_out, x);
  and and_1 (and_1_out, not_1_out, y);
  xor xor_2 (xor_2_out, in_2, in_10);
  xor xor_3 (out_19, and_1_out, xor_2_out);
  not not_2 (not_2_out, in_2);
  and and_2 (and_2_out, not_2_out, in_10);
  and and_3 (and_3_out, and_1_out, not_3_out);
  not not_3 (not_3_out, xor_2_out);
  or or_1 (or_1_out, and_2_out, and_3_out);
  xor xor_4 (xor_4_out, in_3, in_11);
  xor xor_5 (out_20, or_1_out, xor_4_out);
  not not_4 (not_4_out, in_3);
  not not_5 (not_5_out, xor_4_out);
  and and_4 (and_4_out, not_4_out, in_11);
  and and_5 (and_5_out, or_1_out, not_5_out);
  xor xor_6 (xor_6_out, in_4, in_12);
  or or_2 (or_2_out, and_4_out, and_5_out);
  xor xor_7 (out_21, or_2_out, xor_6_out);
  not not_6 (not_6_out, in_4);
  not not_7 (not_7_out, xor_6_out);
  and and_6 (and_6_out, not_6_out, in_12);
  and and_7 (and_7_out, or_2_out, not_7_out);
  or or_3 (or_3_out, and_6_out, and_7_out);
  xor xor_8 (out_22, or_3_out, xor_9_out);
  not not_8 (not_8_out, in_5);
  xor xor_9 (xor_9_out, in_5, in_13);
  not not_9 (not_9_out, xor_9_out);
  and and_8 (and_8_out, not_8_out, in_13);
  and and_9 (and_9_out, or_3_out, not_9_out);
  or or_4 (or_4_out, and_8_out, and_9_out);
  xor xor_10 (out_23, or_4_out, xor_11_out);
  not not_10 (not_10_out, in_6);
  xor xor_11 (xor_11_out, in_6, in_14);
  not not_11 (not_11_out, xor_11_out);
  and and_10 (and_10_out, not_10_out, in_14);
  and and_11 (and_11_out, or_4_out, not_11_out);
  or or_5 (or_5_out, and_10_out, and_11_out);
  not not_12 (not_12_out, in_7);
  xor xor_12 (xor_12_out, in_7, in_15);
  not not_13 (not_13_out, xor_12_out);
  xor xor_13 (out_24, or_5_out, xor_12_out);
  and and_12 (and_12_out, not_12_out, in_15);
  and and_13 (and_13_out, or_5_out, not_13_out);
  or or_6 (or_6_out, and_12_out, and_13_out);
  not not_14 (not_14_out, in_8);
  xor xor_14 (xor_14_out, in_8, in_16);
  not not_15 (not_15_out, xor_14_out);
  xor xor_15 (out_25, or_6_out, xor_14_out);
  and and_14 (and_14_out, not_14_out, in_16);
  and and_15 (and_15_out, or_6_out, not_15_out);
  or or_7 (overflow, and_14_out, and_15_out);
endmodule

module Resto_negativo (
  input  in_1,
  input  in_2,
  input  in_3,
  input  in_4,
  input  in_5,
  input  in_6,
  input  in_7,
  input  in_8,
  input  in_9,
  input  in_10,
  input  in_11,
  input  in_12,
  input  in_13,
  input  in_14,
  input  in_15,
  input  in_16,
  input  in_17,
  output out_18,
  output out_19,
  output out_20,
  output out_21,
  output out_22,
  output out_23,
  output out_24,
  output out_25
);

  wire and_1_out, and_2_out, and_3_out, and_4_out, and_5_out, and_6_out, and_7_out, and_8_out, and_9_out,
       and_10_out, and_11_out, and_12_out, and_13_out, and_14_out, and_15_out, and_16_out, not_1_out, S0, S1,
       S2, S3, S4, S5, S6, S7;

  not not_1 (not_1_out, in_17);
  and and_1 (and_1_out, not_1_out, in_9);
  and and_2 (and_2_out, in_17, S0);
  or or_1 (out_18, and_1_out, and_2_out);
  and and_3 (and_3_out, not_1_out, in_10);
  or or_2 (out_19, and_3_out, and_4_out);
  and and_4 (and_4_out, in_17, S1);
  and and_5 (and_5_out, not_1_out, in_11);
  or or_3 (out_20, and_5_out, and_7_out);
  and and_6 (and_6_out, not_1_out, in_12);
  and and_7 (and_7_out, in_17, S2);
  subtracao_parcial subtracao_parcial_1 (
    .x(in_1), .in_2(in_2), .in_3(in_3), .in_4(in_4), .in_5(in_5), .in_6(in_6), .in_7(in_7), .in_8(in_8),
    .y(in_9), .in_10(in_10), .in_11(in_11), .in_12(in_12), .in_13(in_13), .in_14(in_14), .in_15(in_15),
    .in_16(in_16), .out(S0), .out_19(S1), .out_20(S2), .out_21(S3), .out_22(S4), .out_23(S5), .out_24(S6),
    .out_25(S7));  // open: overflow
  and and_8 (and_8_out, not_1_out, in_13);
  and and_9 (and_9_out, in_17, S3);
  or or_4 (out_21, and_6_out, and_9_out);
  and and_10 (and_10_out, in_17, S4);
  or or_5 (out_22, and_8_out, and_10_out);
  and and_11 (and_11_out, in_17, S5);
  and and_12 (and_12_out, not_1_out, in_14);
  or or_6 (out_23, and_12_out, and_11_out);
  and and_13 (and_13_out, not_1_out, in_15);
  and and_14 (and_14_out, in_17, S6);
  or or_7 (out_24, and_13_out, and_14_out);
  and and_15 (and_15_out, not_1_out, in_16);
  and and_16 (and_16_out, in_17, S7);
  or or_8 (out_25, and_15_out, and_16_out);

  // Other names for the same wires on the sheet: A0 = in_1; A1 = in_2; A2 = in_3; A3 = in_4; A4 = in_5; A5 = in_6;
  //   A6 = in_7; A7 = in_8; B0 = in_9; B1 = in_10; B2 = in_11; B3 = in_12; B4 = in_13; B5 = in_14; B6 = in_15;
  //   B7 = in_16
endmodule
