// Logisim project multiplicacao.circ as structural Verilog: 2 circuits, main circuit main
module main (
  input  in_1,
  input  in_2,
  input  in_3,
  input  in_4,
  input  in_5,
  input  in_6,
  input  in_7,
  input  in_8,
  input  in_9,
  input  in_10,
  input  in_11,
  input  in_12,
  input  in_13,
  input  in_14,
  input  in_15,
  input  in_16,
  output out_17,
  output out_18,
  output out_19,
  output out_20,
  output out_21,
  output out_22,
  output out_23,
  output out_24,
  output out_25
);

  wire _0, _1, _2, _3, _4, _5, _6, _7, auxiliar_1_out_10, auxiliar_1_out_11, auxiliar_1_out_12,
       auxiliar_1_out_13, auxiliar_1_out_14, auxiliar_1_out_15, auxiliar_1_out_16, auxiliar_1_out_17,
       auxiliar_2_out_10, auxiliar_2_out_11, auxiliar_2_out_12, auxiliar_2_out_13, auxiliar_2_out_14,
       auxiliar_2_out_15, auxiliar_2_out_16, auxiliar_2_out_17, auxiliar_3_out_10, auxiliar_3_out_11,
       auxiliar_3_out_12, auxiliar_3_out_13, auxiliar_3_out_14, auxiliar_3_out_15, auxiliar_3_out_16,
       auxiliar_3_out_17, auxiliar_4_out_10, auxiliar_4_out_11, auxiliar_4_out_12, auxiliar_4_out_13,
       auxiliar_4_out_14, auxiliar_4_out_15, auxiliar_4_out_16, auxiliar_4_out_17, auxiliar_5_out_10,
       auxiliar_5_out_11, auxiliar_5_out_12, auxiliar_5_out_13, auxiliar_5_out_14, auxiliar_5_out_15,
       auxiliar_5_out_16, auxiliar_5_out_17, auxiliar_6_out_10, auxiliar_6_out_11, auxiliar_6_out_12,
       auxiliar_6_out_13, auxiliar_6_out_14, auxiliar_6_out_15, auxiliar_6_out_16, auxiliar_6_out_17,
       auxiliar_7_out_10, auxiliar_7_out_11, auxiliar_7_out_12, auxiliar_7_out_13, auxiliar_7_out_14,
       auxiliar_7_out_15, auxiliar_7_out_16, auxiliar_7_out_17, auxiliar_8_out_10, auxiliar_8_out_11,
       auxiliar_8_out_12, auxiliar_8_out_13, auxiliar_8_out_14, auxiliar_8_out_15, auxiliar_8_out_16,
       auxiliar_8_out_17, C0, C1, C2, C3, C4, C5, C6, E0, E1, E2, E3, E4, E5, E6, E7, not_1_out, OVERFLOW1,
       OVERFLOW2, S0, S1, S2, S3, S4, S5, S6, S7, soma_1_out_18, soma_1_out_19, soma_1_out_20, soma_1_out_21,
       soma_1_out_22, soma_1_out_23, soma_1_out_24, soma_2_out_18, soma_2_out_19, soma_2_out_20,
       soma_2_out_21, soma_2_out_22, soma_2_out_23, soma_2_out_24, soma_3_out_18, soma_3_out_19,
       soma_3_out_20, soma_3_out_21, soma_3_out_22, soma_3_out_23, soma_3_out_24, soma_4_out_18,
       soma_4_out_19, soma_4_out_20, soma_4_out_21, soma_4_out_22, soma_4_out_23, soma_4_out_24,
       soma_5_out_18, soma_5_out_19, soma_5_out_20, soma_5_out_21, soma_5_out_22, soma_5_out_23,
       soma_5_out_24, soma_6_out_18, soma_6_out_19, soma_6_out_20, soma_6_out_21, soma_6_out_22,
       soma_6_out_23, soma_6_out_24, soma_7_out_18, soma_7_out_19, soma_7_out_20, soma_7_out_21,
       soma_7_out_22, soma_7_out_23, soma_7_out_24, soma_7_overflow, soma_8_out_18, soma_8_out_19,
       soma_8_out_20, soma_8_out_21, soma_8_out_22, soma_8_out_23, soma_8_out_24, xor_1_out;

  soma soma_1 (
    .X(soma_8_out_18), .Y(auxiliar_3_out_10), .in_2(soma_8_out_19), .in_10(auxiliar_3_out_11),
    .in_3(soma_8_out_20), .in_11(auxiliar_3_out_12), .in_4(soma_8_out_21), .in_12(auxiliar_3_out_13),
    .in_5(soma_8_out_22), .in_13(auxiliar_3_out_14), .in_6(soma_8_out_23), .in_14(auxiliar_3_out_15),
    .in_7(soma_8_out_24), .in_15(auxiliar_3_out_16), .in_8(C0), .in_16(auxiliar_3_out_17), .Z(S1),
    .out_18(soma_1_out_18), .out_19(soma_1_out_19), .out_20(soma_1_out_20), .out_21(soma_1_out_21),
    .out_22(soma_1_out_22), .out_23(soma_1_out_23), .out_24(soma_1_out_24), .Overflow(C1));
  soma soma_2 (
    .X(soma_1_out_18), .Y(auxiliar_4_out_10), .in_2(soma_1_out_19), .in_10(auxiliar_4_out_11),
    .in_3(soma_1_out_20), .in_11(auxiliar_4_out_12), .in_4(soma_1_out_21), .in_12(auxiliar_4_out_13),
    .in_5(soma_1_out_22), .in_13(auxiliar_4_out_14), .in_6(soma_1_out_23), .in_14(auxiliar_4_out_15),
    .in_7(soma_1_out_24), .in_15(auxiliar_4_out_16), .in_8(C1), .in_16(auxiliar_4_out_17), .Z(S2),
    .out_18(soma_2_out_18), .out_19(soma_2_out_19), .out_20(soma_2_out_20), .out_21(soma_2_out_21),
    .out_22(soma_2_out_22), .out_23(soma_2_out_23), .out_24(soma_2_out_24), .Overflow(C2));
  soma soma_3 (
    .X(soma_2_out_18), .Y(auxiliar_5_out_10), .in_2(soma_2_out_19), .in_10(auxiliar_5_out_11),
    .in_3(soma_2_out_20), .in_11(auxiliar_5_out_12), .in_4(soma_2_out_21), .in_12(auxiliar_5_out_13),
    .in_5(soma_2_out_22), .in_13(auxiliar_5_out_14), .in_6(soma_2_out_23), .in_14(auxiliar_5_out_15),
    .in_7(soma_2_out_24), .in_15(auxiliar_5_out_16), .in_8(C2), .in_16(auxiliar_5_out_17), .Z(S3),
    .out_18(soma_3_out_18), .out_19(soma_3_out_19), .out_20(soma_3_out_20), .out_21(soma_3_out_21),
    .out_22(soma_3_out_22), .out_23(soma_3_out_23), .out_24(soma_3_out_24), .Overflow(C3));
  soma soma_4 (
    .X(soma_3_out_18), .Y(auxiliar_6_out_10), .in_2(soma_3_out_19), .in_10(auxiliar_6_out_11),
    .in_3(soma_3_out_20), .in_11(auxiliar_6_out_12), .in_4(soma_3_out_21), .in_12(auxiliar_6_out_13),
    .in_5(soma_3_out_22), .in_13(auxiliar_6_out_14), .in_6(soma_3_out_23), .in_14(auxiliar_6_out_15),
    .in_7(soma_3_out_24), .in_15(auxiliar_6_out_16), .in_8(C3), .in_16(auxiliar_6_out_17), .Z(S4),
    .out_18(soma_4_out_18), .out_19(soma_4_out_19), .out_20(soma_4_out_20), .out_21(soma_4_out_21),
    .out_22(soma_4_out_22), .out_23(soma_4_out_23), .out_24(soma_4_out_24), .Overflow(C4));
  soma soma_5 (
    .X(soma_4_out_18), .Y(auxiliar_7_out_10), .in_2(soma_4_out_19), .in_10(auxiliar_7_out_11),
    .in_3(soma_4_out_20), .in_11(auxiliar_7_out_12), .in_4(soma_4_out_21), .in_12(auxiliar_7_out_13),
    .in_5(soma_4_out_22), .in_13(auxiliar_7_out_14), .in_6(soma_4_out_23), .in_14(auxiliar_7_out_15),
    .in_7(soma_4_out_24), .in_15(auxiliar_7_out_16), .in_8(C4), .in_16(auxiliar_7_out_17), .Z(S5),
    .out_18(soma_5_out_18), .out_19(soma_5_out_19), .out_20(soma_5_out_20), .out_21(soma_5_out_21),
    .out_22(soma_5_out_22), .out_23(soma_5_out_23), .out_24(soma_5_out_24), .Overflow(C5));
  soma soma_6 (
    .X(soma_5_out_18), .Y(auxiliar_8_out_10), .in_2(soma_5_out_19), .in_10(auxiliar_8_out_11),
    .in_3(soma_5_out_20), .in_11(auxiliar_8_out_12), .in_4(soma_5_out_21), .in_12(auxiliar_8_out_13),
    .in_5(soma_5_out_22), .in_13(auxiliar_8_out_14), .in_6(soma_5_out_23), .in_14(auxiliar_8_out_15),
    .in_7(soma_5_out_24), .in_15(auxiliar_8_out_16), .in_8(C5), .in_16(auxiliar_8_out_17), .Z(S6),
    .out_18(soma_6_out_18), .out_19(soma_6_out_19), .out_20(soma_6_out_20), .out_21(soma_6_out_21),
    .out_22(soma_6_out_22), .out_23(soma_6_out_23), .out_24(soma_6_out_24), .Overflow(C6));
  soma soma_7 (
    .X(soma_6_out_18), .Y(auxiliar_1_out_10), .in_2(soma_6_out_19), .in_10(auxiliar_1_out_11),
    .in_3(soma_6_out_20), .in_11(auxiliar_1_out_12), .in_4(soma_6_out_21), .in_12(auxiliar_1_out_13),
    .in_5(soma_6_out_22), .in_13(auxiliar_1_out_14), .in_6(soma_6_out_23), .in_14(auxiliar_1_out_15),
    .in_7(soma_6_out_24), .in_15(auxiliar_1_out_16), .in_8(C6), .in_16(auxiliar_1_out_17), .Z(S7),
    .out_18(soma_7_out_18), .out_19(soma_7_out_19), .out_20(soma_7_out_20), .out_21(soma_7_out_21),
    .out_22(soma_7_out_22), .out_23(soma_7_out_23), .out_24(soma_7_out_24), .Overflow(soma_7_overflow));
  soma soma_8 (
    .X(1'b0), .Y(auxiliar_2_out_10), .in_2(1'b0), .in_10(auxiliar_2_out_11), .in_3(1'b0),
    .in_11(auxiliar_2_out_12), .in_4(1'b0), .in_12(auxiliar_2_out_13), .in_5(1'b0),
    .in_13(auxiliar_2_out_14), .in_6(1'b0), .in_14(auxiliar_2_out_15), .in_7(1'b0),
    .in_15(auxiliar_2_out_16), .in_8(1'b0), .in_16(auxiliar_2_out_17), .Z(S0), .out_18(soma_8_out_18),
    .out_19(soma_8_out_19), .out_20(soma_8_out_20), .out_21(soma_8_out_21), .out_22(soma_8_out_22),
    .out_23(soma_8_out_23), .out_24(soma_8_out_24), .Overflow(C0));
  auxiliar auxiliar_1 (
    .in_9(E7), .in_1(_0), .in_2(_1), .in_3(_2), .in_4(_3), .in_5(_4), .in_6(_5), .in_7(_6), .in_8(_7),
    .out_10(auxiliar_1_out_10), .out_11(auxiliar_1_out_11), .out_12(auxiliar_1_out_12),
    .out_13(auxiliar_1_out_13), .out_14(auxiliar_1_out_14), .out_15(auxiliar_1_out_15),
    .out_16(auxiliar_1_out_16), .out_17(auxiliar_1_out_17));
  or or_1 (OVERFLOW1, soma_7_out_24, soma_7_out_23, soma_7_out_22, soma_7_out_21, soma_7_out_20, soma_7_out_19, soma_7_out_18, soma_7_overflow);
  auxiliar auxiliar_2 (
    .in_9(E0), .in_1(_0), .in_2(_1), .in_3(_2), .in_4(_3), .in_5(_4), .in_6(_5), .in_7(_6), .in_8(_7),
    .out_10(auxiliar_2_out_10), .out_11(auxiliar_2_out_11), .out_12(auxiliar_2_out_12),
    .out_13(auxiliar_2_out_13), .out_14(auxiliar_2_out_14), .out_15(auxiliar_2_out_15),
    .out_16(auxiliar_2_out_16), .out_17(auxiliar_2_out_17));
  auxiliar auxiliar_3 (
    .in_9(E1), .in_1(_0), .in_2(_1), .in_3(_2), .in_4(_3), .in_5(_4), .in_6(_5), .in_7(_6), .in_8(_7),
    .out_10(auxiliar_3_out_10), .out_11(auxiliar_3_out_11), .out_12(auxiliar_3_out_12),
    .out_13(auxiliar_3_out_13), .out_14(auxiliar_3_out_14), .out_15(auxiliar_3_out_15),
    .out_16(auxiliar_3_out_16), .out_17(auxiliar_3_out_17));
  auxiliar auxiliar_4 (
    .in_9(E2), .in_1(_0), .in_2(_1), .in_3(_2), .in_4(_3), .in_5(_4), .in_6(_5), .in_7(_6), .in_8(_7),
    .out_10(auxiliar_4_out_10), .out_11(auxiliar_4_out_11), .out_12(auxiliar_4_out_12),
    .out_13(auxiliar_4_out_13), .out_14(auxiliar_4_out_14), .out_15(auxiliar_4_out_15),
    .out_16(auxiliar_4_out_16), .out_17(auxiliar_4_out_17));
  auxiliar auxiliar_5 (
    .in_9(E3), .in_1(_0), .in_2(_1), .in_3(_2), .in_4(_3), .in_5(_4), .in_6(_5), .in_7(_6), .in_8(_7),
    .out_10(auxiliar_5_out_10), .out_11(auxiliar_5_out_11), .out_12(auxiliar_5_out_12),
    .out_13(auxiliar_5_out_13), .out_14(auxiliar_5_out_14), .out_15(auxiliar_5_out_15),
    .out_16(auxiliar_5_out_16), .out_17(auxiliar_5_out_17));
  auxiliar auxiliar_6 (
    .in_9(E4), .in_1(_0), .in_2(_1), .in_3(_2), .in_4(_3), .in_5(_4), .in_6(_5), .in_7(_6), .in_8(_7),
    .out_10(auxiliar_6_out_10), .out_11(auxiliar_6_out_11), .out_12(auxiliar_6_out_12),
    .out_13(auxiliar_6_out_13), .out_14(auxiliar_6_out_14), .out_15(auxiliar_6_out_15),
    .out_16(auxiliar_6_out_16), .out_17(auxiliar_6_out_17));
  auxiliar auxiliar_7 (
    .in_9(E5), .in_1(_0), .in_2(_1), .in_3(_2), .in_4(_3), .in_5(_4), .in_6(_5), .in_7(_6), .in_8(_7),
    .out_10(auxiliar_7_out_10), .out_11(auxiliar_7_out_11), .out_12(auxiliar_7_out_12),
    .out_13(auxiliar_7_out_13), .out_14(auxiliar_7_out_14), .out_15(auxiliar_7_out_15),
    .out_16(auxiliar_7_out_16), .out_17(auxiliar_7_out_17));
  auxiliar auxiliar_8 (
    .in_9(E6), .in_1(_0), .in_2(_1), .in_3(_2), .in_4(_3), .in_5(_4), .in_6(_5), .in_7(_6), .in_8(_7),
    .out_10(auxiliar_8_out_10), .out_11(auxiliar_8_out_11), .out_12(auxiliar_8_out_12),
    .out_13(auxiliar_8_out_13), .out_14(auxiliar_8_out_14), .out_15(auxiliar_8_out_15),
    .out_16(auxiliar_8_out_16), .out_17(auxiliar_8_out_17));
  or or_2 (out_17, OVERFLOW1, OVERFLOW2);
  xor xor_1 (xor_1_out, in_8, in_16);
  inversor_main main_1 (
    .in_1(in_1), .in_2(in_2), .in_3(in_3), .in_4(in_4), .in_5(in_5), .in_6(in_6), .in_7(in_7), .in_8(in_8),
    .in_9(in_8), .out_10(_0), .out_11(_1), .out_12(_2), .out_13(_3), .out_14(_4), .out_15(_5), .out_16(_6),
    .out_17(_7));
  inversor_main main_2 (
    .in_1(in_9), .in_2(in_10), .in_3(in_11), .in_4(in_12), .in_5(in_13), .in_6(in_14), .in_7(in_15),
    .in_8(in_16), .in_9(in_16), .out_10(E0), .out_11(E1), .out_12(E2), .out_13(E3), .out_14(E4), .out_15(E5),
    .out_16(E6), .out_17(E7));
  inversor_main main_3 (
    .in_1(S0), .in_2(S1), .in_3(S2), .in_4(S3), .in_5(S4), .in_6(S5), .in_7(S6), .in_8(S7), .in_9(xor_1_out),
    .out_10(out_18), .out_11(out_19), .out_12(out_20), .out_13(out_21), .out_14(out_22), .out_15(out_23),
    .out_16(out_24), .out_17(out_25));
  not not_1 (not_1_out, xor_1_out);
  and and_1 (OVERFLOW2, not_1_out, out_25);

  // Other names for the same wires on the sheet: I1 = in_8; I2 = in_16
endmodule

module auxiliar (
  input  in_1,
  input  in_2,
  input  in_3,
  input  in_4,
  input  in_5,
  input  in_6,
  input  in_7,
  input  in_8,
  input  in_9,
  output out_10,
  output out_11,
  output out_12,
  output out_13,
  output out_14,
  output out_15,
  output out_16,
  output out_17
);

  and and_1 (out_10, in_1, in_9);
  and and_2 (out_11, in_2, in_9);
  and and_3 (out_12, in_3, in_9);
  and and_4 (out_14, in_5, in_9);
  and and_5 (out_13, in_4, in_9);
  and and_6 (out_15, in_6, in_9);
  and and_7 (out_16, in_7, in_9);
  and and_8 (out_17, in_8, in_9);
endmodule
