// Logisim project mainALU.circ as structural Verilog: 1 circuit, main circuit main
module main (
  input  Mais_significativo,
  input  in_2,
  input  in_3,
  input  in_4,
  input  in_5,
  input  in_6,
  input  in_7,
  input  in_8,
  input  Mais_significativo_2,
  input  in_10,
  input  in_11,
  input  in_12,
  input  in_13,
  input  in_14,
  input  in_15,
  input  in_16,
  input  in_17,
  input  in_18,
  input  in_19,
  output Mais_significativo_3,
  output out_21,
  output out_22,
  output out_23,
  output out_24,
  output out_25,
  output out_26,
  output out_27,
  output out_28
);

  wire minus_OVERFLOW, OVERFLOW, plus_OVERFLOW;
  wire [7:0] A, B, demultiplexer_1_out3, demultiplexer_1_out4, demultiplexer_2_out3, demultiplexer_2_out4,
       minus_A, minus_B, minus_R, nA, nB, nR, plus_A, plus_B, plus_R, R, R_t;

  soma SOMA (
    .X(plus_A[7]), .Y(plus_B[7]), .in_2(plus_A[6]), .in_10(plus_B[6]), .in_3(plus_A[5]), .in_11(plus_B[5]),
    .in_4(plus_A[4]), .in_12(plus_B[4]), .in_5(plus_A[3]), .in_13(plus_B[3]), .in_6(plus_A[2]),
    .in_14(plus_B[2]), .in_7(plus_A[1]), .in_15(plus_B[1]), .in_8(plus_A[0]), .in_16(plus_B[0]),
    .Z(plus_R[7]), .out_18(plus_R[6]), .out_19(plus_R[5]), .out_20(plus_R[4]), .out_21(plus_R[3]),
    .out_22(plus_R[2]), .out_23(plus_R[1]), .out_24(plus_R[0]), .out_25(plus_OVERFLOW));
  subtracVfinale_main SUBTRACAO (
    .x(minus_A[7]), .y(minus_B[7]), .out(minus_R[7]), .in_2(minus_A[6]), .in_10(minus_B[6]),
    .out_19(minus_R[6]), .in_3(minus_A[5]), .in_11(minus_B[5]), .out_20(minus_R[5]), .in_4(minus_A[4]),
    .in_12(minus_B[4]), .out_21(minus_R[4]), .in_5(minus_A[3]), .in_13(minus_B[3]), .out_22(minus_R[3]),
    .in_6(minus_A[2]), .in_14(minus_B[2]), .out_23(minus_R[2]), .in_7(minus_A[1]), .in_15(minus_B[1]),
    .out_24(minus_R[1]), .in_8(minus_A[0]), .in_16(minus_B[0]), .out_25(minus_R[0]), .overflow(minus_OVERFLOW));
  Demultiplexer #(.select(3), .width(8), .enable("false")) demultiplexer_1 (
    .out0(plus_A), .out1(minus_A), .out2(A), .out3(demultiplexer_1_out3), .out4(demultiplexer_1_out4),
    .in({in_8, in_7, in_6, in_5, in_4, in_3, in_2, Mais_significativo}), .sel({in_17, in_18, in_19}));  // open: out5, out6, out7
  Demultiplexer #(.select(3), .width(8), .enable("false")) demultiplexer_2 (
    .out0(plus_B), .out1(minus_B), .out2(B), .out3(demultiplexer_2_out3), .out4(demultiplexer_2_out4),
    .in({in_16, in_15, in_14, in_13, in_12, in_11, in_10, Mais_significativo_2}), .sel({in_17, in_18, in_19}));  // open: out5, out6, out7
  assign nA = demultiplexer_1_out3 | demultiplexer_1_out4;  // OR_Gate or_1, 8 bits wide
  assign nB = demultiplexer_2_out3 | demultiplexer_2_out4;  // OR_Gate or_2, 8 bits wide
  divider_main DIVISAO_RESTO (
    .in_1(nA[7]), .in_2(nA[6]), .in_3(nA[5]), .in_4(nA[4]), .in_5(nA[3]), .in_6(nA[2]), .in_7(nA[1]),
    .in_8(nA[0]), .in_9(nB[7]), .in_10(nB[6]), .in_11(nB[5]), .in_12(nB[4]), .in_13(nB[3]), .in_14(nB[2]),
    .in_15(nB[1]), .in_16(nB[0]), .out_17(nR[7]), .out_18(nR[6]), .out_19(nR[5]), .out_20(nR[4]),
    .out_21(nR[3]), .out_22(nR[2]), .out_23(nR[1]), .out_24(nR[0]), .out_25(R[7]), .out_26(R[6]),
    .out_27(R[5]), .out_28(R[4]), .out_29(R[3]), .out_30(R[2]), .out_31(R[1]), .out_32(R[0]));
  or or_3 (out_28, plus_OVERFLOW, minus_OVERFLOW, OVERFLOW);
  Multiplexer #(.select(3), .width(8), .enable("false")) multiplexer_1 (
    .in0(plus_R), .in1(minus_R), .in2(R_t), .in3(nR), .in4(R),
    .out({out_27, out_26, out_25, out_24, out_23, out_22, out_21, Mais_significativo_3}),
    .sel({in_17, in_18, in_19}));  // open: in5, in6, in7
  multiplier_main MULTIPLICACAO (
    .out_17(OVERFLOW), .in_1(A[7]), .in_9(B[7]), .out_18(R_t[7]), .in_2(A[6]), .in_10(B[6]), .out_19(R_t[6]),
    .in_3(A[5]), .in_4(A[4]), .in_11(B[5]), .out_20(R_t[5]), .in_5(A[3]), .in_12(B[4]), .out_21(R_t[4]),
    .in_6(A[2]), .in_7(A[1]), .in_13(B[3]), .out_22(R_t[3]), .in_8(A[0]), .in_14(B[2]), .out_23(R_t[2]),
    .in_15(B[1]), .out_24(R_t[1]), .in_16(B[0]), .out_25(R_t[0]));

  // Other names for the same wires on the sheet: A_t[7:0] = {in_8, in_7, in_6, in_5, in_4, in_3, in_2, Mais_significativo};
  //   B_t[7:0] = {in_16, in_15, in_14, in_13, in_12, in_11, in_10, Mais_significativo_2}; OVERFLOW_t = out_28;
  //   R_t_t[7:0] = {out_27, out_26, out_25, out_24, out_23, out_22, out_21, Mais_significativo_3};
  //   SEL[2:0] = {in_17, in_18, in_19}
endmodule
