// Logisim project dividerBySesso.circ as structural Verilog: 1 circuit, main circuit main
module main (
  input  in_1,
  input  in_2,
  input  in_3,
  input  in_4,
  input  in_5,
  input  in_6,
  input  in_7,
  input  in_8,
  input  in_9,
  input  in_10,
  input  in_11,
  input  in_12,
  input  in_13,
  input  in_14,
  input  in_15,
  input  in_16,
  output out_17,
  output out_18,
  output out_19,
  output out_20,
  output out_21,
  output out_22,
  output out_23,
  output out_24,
  output out_25,
  output out_26,
  output out_27,
  output out_28,
  output out_29,
  output out_30,
  output out_31,
  output out_32
);

  wire main_1_out_17, main_2_out_17, main_2_out_18, main_3_out_17, main_3_out_18, main_3_out_19,
       main_4_out_17, main_4_out_18, main_4_out_19, main_4_out_20, main_5_out_17, main_5_out_18,
       main_5_out_19, main_5_out_20, main_5_out_21, main_6_out_17, main_6_out_18, main_6_out_19,
       main_6_out_20, main_6_out_21, main_6_out_22, main_7_out_17, main_7_out_18, main_7_out_19,
       main_7_out_20, main_7_out_21, main_7_out_22, main_7_out_23;

  subParaDiv_main main_1 (
    .in_1(in_8), .in_2(1'b0), .in_3(1'b0), .in_4(1'b0), .in_5(1'b0), .in_6(1'b0), .in_7(1'b0), .in_8(1'b0),
    .in_9(in_9), .in_10(in_10), .in_11(in_11), .in_12(in_12), .in_13(in_13), .in_14(in_14), .in_15(in_15),
    .in_16(in_16), .out_17(main_1_out_17), .out_25(out_24));  // open: out_18, out_19, out_20, out_21, out_22, out_23, out_24
  subParaDiv_main main_2 (
    .in_1(in_7), .in_2(main_1_out_17), .in_3(1'b0), .in_4(1'b0), .in_5(1'b0), .in_6(1'b0), .in_7(1'b0),
    .in_8(1'b0), .in_9(in_9), .in_10(in_10), .in_11(in_11), .in_12(in_12), .in_13(in_13), .in_14(in_14),
    .in_15(in_15), .in_16(in_16), .out_17(main_2_out_17), .out_18(main_2_out_18), .out_25(out_23));  // open: out_19, out_20, out_21, out_22, out_23, out_24
  subParaDiv_main main_3 (
    .in_1(in_6), .in_2(main_2_out_17), .in_3(main_2_out_18), .in_4(1'b0), .in_5(1'b0), .in_6(1'b0),
    .in_7(1'b0), .in_8(1'b0), .in_9(in_9), .in_10(in_10), .in_11(in_11), .in_12(in_12), .in_13(in_13),
    .in_14(in_14), .in_15(in_15), .in_16(in_16), .out_17(main_3_out_17), .out_18(main_3_out_18),
    .out_19(main_3_out_19), .out_25(out_22));  // open: out_20, out_21, out_22, out_23, out_24
  subParaDiv_main main_4 (
    .in_1(in_5), .in_2(main_3_out_17), .in_3(main_3_out_18), .in_4(main_3_out_19), .in_5(1'b0), .in_6(1'b0),
    .in_7(1'b0), .in_8(1'b0), .in_9(in_9), .in_10(in_10), .in_11(in_11), .in_12(in_12), .in_13(in_13),
    .in_14(in_14), .in_15(in_15), .in_16(in_16), .out_17(main_4_out_17), .out_18(main_4_out_18),
    .out_19(main_4_out_19), .out_20(main_4_out_20), .out_25(out_21));  // open: out_21, out_22, out_23, out_24
  subParaDiv_main main_5 (
    .in_1(in_4), .in_2(main_4_out_17), .in_3(main_4_out_18), .in_4(main_4_out_19), .in_5(main_4_out_20),
    .in_6(1'b0), .in_7(1'b0), .in_8(1'b0), .in_9(in_9), .in_10(in_10), .in_11(in_11), .in_12(in_12),
    .in_13(in_13), .in_14(in_14), .in_15(in_15), .in_16(in_16), .out_17(main_5_out_17),
    .out_18(main_5_out_18), .out_19(main_5_out_19), .out_20(main_5_out_20), .out_21(main_5_out_21),
    .out_25(out_20));  // open: out_22, out_23, out_24
  subParaDiv_main main_6 (
    .in_1(in_3), .in_2(main_5_out_17), .in_3(main_5_out_18), .in_4(main_5_out_19), .in_5(main_5_out_20),
    .in_6(main_5_out_21), .in_7(1'b0), .in_8(1'b0), .in_9(in_9), .in_10(in_10), .in_11(in_11), .in_12(in_12),
    .in_13(in_13), .in_14(in_14), .in_15(in_15), .in_16(in_16), .out_17(main_6_out_17),
    .out_18(main_6_out_18), .out_19(main_6_out_19), .out_20(main_6_out_20), .out_21(main_6_out_21),
    .out_22(main_6_out_22), .out_25(out_19));  // open: out_23, out_24
  subParaDiv_main main_7 (
    .in_1(in_2), .in_2(main_6_out_17), .in_3(main_6_out_18), .in_4(main_6_out_19), .in_5(main_6_out_20),
    .in_6(main_6_out_21), .in_7(main_6_out_22), .in_8(1'b0), .in_9(in_9), .in_10(in_10), .in_11(in_11),
    .in_12(in_12), .in_13(in_13), .in_14(in_14), .in_15(in_15), .in_16(in_16), .out_17(main_7_out_17),
    .out_18(main_7_out_18), .out_19(main_7_out_19), .out_20(main_7_out_20), .out_21(main_7_out_21),
    .out_22(main_7_out_22), .out_23(main_7_out_23), .out_25(out_18));  // open: out_24
  subParaDiv_main main_8 (
    .in_1(in_1), .in_2(main_7_out_17), .in_3(main_7_out_18), .in_4(main_7_out_19), .in_5(main_7_out_20),
    .in_6(main_7_out_21), .in_7(main_7_out_22), .in_8(main_7_out_23), .in_9(in_9), .in_10(in_10),
    .in_11(in_11), .in_12(in_12), .in_13(in_13), .in_14(in_14), .in_15(in_15), .in_16(in_16),
    .out_17(out_25), .out_18(out_26), .out_19(out_27), .out_20(out_28), .out_21(out_29), .out_22(out_30),
    .out_23(out_31), .out_24(out_32), .out_25(out_17));

  // Other names for the same wires on the sheet: A0 = in_1; A1 = in_2; A2 = in_3; A3 = in_4; A4 = in_5; A5 = in_6;
  //   A6 = in_7; A7 = in_8; B0 = in_9; B1 = in_10; B2 = in_11; B3 = in_12; B4 = in_13; B5 = in_14; B6 = in_15;
  //   B7 = in_16; Q0 = out_17; Q1 = out_18; Q2 = out_19; Q3 = out_20; Q4 = out_21; Q5 = out_22; Q6 = out_23;
  //   Q7 = out_24; R0 = out_25; R1 = out_26; R2 = out_27; R3 = out_28; R4 = out_29; R5 = out_30; R6 = out_31;
  //   R7 = out_32
endmodule
