// Logisim project dividerByStar.circ as structural Verilog: 3 circuits, main circuit main
module main (
  input  in_1,
  input  in_2,
  input  in_3,
  input  in_4,
  input  in_5,
  input  in_6,
  input  in_7,
  input  in_8,
  input  in_9,
  input  in_10,
  input  in_11,
  input  in_12,
  input  in_13,
  input  in_14,
  input  in_15,
  input  in_16,
  input  in_17,
  output out_18,
  output out_19,
  output out_20,
  output out_21,
  output out_22,
  output out_23,
  output out_24,
  output out_25
);

  wire Clock, counter_1_out_2, counter_1_out_3, counter_1_out_4, counter_1_out_5, counter_1_out_6,
       counter_1_out_7, counter_1_out_8, counter_1_out_9, main_2_out_18, main_2_out_19, main_2_out_20,
       main_2_out_21, main_2_out_22, main_2_out_23, main_2_out_24, main_2_out_25, not_1_out, Ready,
       soma_1_out_18, soma_1_out_19, soma_1_out_20, soma_1_out_21, soma_1_out_22, soma_1_out_23,
       soma_1_out_24, soma_1_z;

  not not_1 (not_1_out, Ready);
  and and_1 (Clock, in_17, not_1_out);
  counter counter_1 (
    .out_2(counter_1_out_2), .out_3(counter_1_out_3), .in_1(Clock), .out_4(counter_1_out_4),
    .out_5(counter_1_out_5), .out_6(counter_1_out_6), .out_7(counter_1_out_7), .out_8(counter_1_out_8),
    .out_9(counter_1_out_9));
  soma soma_1 (
    .X(main_2_out_18), .Y(in_1), .in_2(main_2_out_19), .in_10(in_2), .in_3(main_2_out_20), .in_11(in_3),
    .in_4(main_2_out_21), .in_12(in_4), .in_5(main_2_out_22), .in_13(in_5), .in_6(main_2_out_23),
    .in_14(in_6), .in_7(main_2_out_24), .in_15(in_7), .in_8(main_2_out_25), .in_16(in_8), .Z(soma_1_z),
    .out_18(soma_1_out_18), .out_19(soma_1_out_19), .out_20(soma_1_out_20), .out_21(soma_1_out_21),
    .out_22(soma_1_out_22), .out_23(soma_1_out_23), .out_24(soma_1_out_24));  // open: out_25
  subtracVfinale_main main_1 (
    .x(in_9), .y(soma_1_z), .in_2(in_10), .in_10(soma_1_out_18), .in_3(in_11), .in_11(soma_1_out_19),
    .in_4(in_12), .in_12(soma_1_out_20), .in_5(in_13), .in_13(soma_1_out_21), .in_6(in_14),
    .in_14(soma_1_out_22), .in_7(in_15), .in_15(soma_1_out_23), .in_8(in_16), .in_16(soma_1_out_24),
    .overflow(Ready));  // open: out, out_19, out_20, out_21, out_22, out_23, out_24, out_25
  multiplier_main main_2 (
    .in_1(counter_1_out_2), .in_9(in_1), .out_18(main_2_out_18), .in_2(counter_1_out_3), .in_10(in_2),
    .out_19(main_2_out_19), .in_3(counter_1_out_4), .in_4(counter_1_out_5), .in_11(in_3),
    .out_20(main_2_out_20), .in_5(counter_1_out_6), .in_12(in_4), .out_21(main_2_out_21),
    .in_6(counter_1_out_7), .in_7(counter_1_out_8), .in_13(in_5), .out_22(main_2_out_22),
    .in_8(counter_1_out_9), .in_14(in_6), .out_23(main_2_out_23), .in_15(in_7), .out_24(main_2_out_24),
    .in_16(in_8), .out_25(main_2_out_25));  // open: out_17
  holder holder_1 (
    .in_9(Clock), .in_1(counter_1_out_2), .in_2(counter_1_out_3), .in_3(counter_1_out_4),
    .in_4(counter_1_out_5), .in_5(counter_1_out_6), .in_6(counter_1_out_7), .in_7(counter_1_out_8),
    .in_8(counter_1_out_9), .out_10(out_18), .out_11(out_19), .out_12(out_20), .out_13(out_21),
    .out_14(out_22), .out_15(out_23), .out_16(out_24), .out_17(out_25));

  // Other names for the same wires on the sheet: A0 = in_9; A1 = in_10; A2 = in_11; A3 = in_12; A4 = in_13;
  //   A5 = in_14; A6 = in_15; A7 = in_16; B0 = in_1; B1 = in_2; B2 = in_3; B3 = in_4; B4 = in_5; B5 = in_6; B6 = in_7;
  //   B7 = in_8

  // Notes on the sheet:
  //   subtração
  //   multiplicação
endmodule

module counter (
  input  in_1,
  output out_2,
  output out_3,
  output out_4,
  output out_5,
  output out_6,
  output out_7,
  output out_8,
  output out_9
);

  wire and_1_out, and_2_out, and_3_out, and_4_out, and_5_out, and_6_out;

  J_K_Flip_Flop j_k_ff_1 (.J(1'b1), .clk(in_1), .K(1'b1), .Q(out_2));  // open: Qn, preset, en, reset
  J_K_Flip_Flop j_k_ff_2 (.J(out_2), .clk(in_1), .K(out_2), .Q(out_3));  // open: Qn, preset, en, reset
  and and_1 (and_1_out, out_3, out_2);
  J_K_Flip_Flop j_k_ff_3 (.J(and_1_out), .clk(in_1), .K(and_1_out), .Q(out_4));  // open: Qn, preset, en, reset
  and and_2 (and_2_out, out_2, out_3, out_4);
  J_K_Flip_Flop j_k_ff_4 (.J(and_2_out), .clk(in_1), .K(and_2_out), .Q(out_5));  // open: Qn, preset, en, reset
  and and_3 (and_3_out, out_2, out_3, out_4, out_5);
  J_K_Flip_Flop j_k_ff_5 (.J(and_3_out), .clk(in_1), .K(and_3_out), .Q(out_6));  // open: Qn, preset, en, reset
  and and_4 (and_4_out, out_2, out_3, out_4, out_5, out_6);
  J_K_Flip_Flop j_k_ff_6 (.J(and_4_out), .clk(in_1), .K(and_4_out), .Q(out_7));  // open: Qn, preset, en, reset
  and and_5 (and_5_out, out_2, out_3, out_4, out_5, out_6, out_7);
  J_K_Flip_Flop j_k_ff_7 (.J(and_5_out), .clk(in_1), .K(and_5_out), .Q(out_8));  // open: Qn, preset, en, reset
  and and_6 (and_6_out, out_8, out_2, out_3, out_4, out_5, out_6, out_7);
  J_K_Flip_Flop j_k_ff_8 (.J(and_6_out), .clk(in_1), .K(and_6_out), .Q(out_9));  // open: Qn, preset, en, reset
endmodule

module holder (
  input  in_1,
  input  in_2,
  input  in_3,
  input  in_4,
  input  in_5,
  input  in_6,
  input  in_7,
  input  in_8,
  input  in_9,
  output out_10,
  output out_11,
  output out_12,
  output out_13,
  output out_14,
  output out_15,
  output out_16,
  output out_17
);

  D_Flip_Flop d_ff_1 (.clk(in_9), .D(in_1), .Q(out_10));  // open: Qn, preset, en, reset
  D_Flip_Flop d_ff_2 (.clk(in_9), .D(in_2), .Q(out_11));  // open: Qn, preset, en, reset
  D_Flip_Flop d_ff_3 (.clk(in_9), .D(in_3), .Q(out_12));  // open: Qn, preset, en, reset
  D_Flip_Flop d_ff_4 (.clk(in_9), .D(in_4), .Q(out_13));  // open: Qn, preset, en, reset
  D_Flip_Flop d_ff_5 (.clk(in_9), .D(in_5), .Q(out_14));  // open: Qn, preset, en, reset
  D_Flip_Flop d_ff_6 (.clk(in_9), .D(in_6), .Q(out_15));  // open: Qn, preset, en, reset
  D_Flip_Flop d_ff_7 (.clk(in_9), .D(in_7), .Q(out_16));  // open: Qn, preset, en, reset
  D_Flip_Flop d_ff_8 (.clk(in_9), .D(in_8), .Q(out_17));  // open: Qn, preset, en, reset
endmodule
