// Logisim project multiplyerByStar.circ as structural Verilog: 2 circuits, main circuit main
module main (
  input  A1,
  input  B1,
  input  A0,
  input  B0,
  output out_5
);

  wire and_1_out, and_2_out;

  and and_1 (and_1_out, A1, B0);
  halfadder halfadder_1 (.in_1(and_2_out), .in_2(and_1_out));  // open: out_3, out_4
  and and_2 (and_2_out, B1, A0);
  and and_3 (out_5, A0, B0);
endmodule

module halfadder (
  input  in_1,
  input  in_2,
  output out_3,
  output out_4
);

  xor xor_1 (out_3, in_1, in_2);
  and and_1 (out_4, in_2, in_1);
endmodule
