// Logisim project Controlador.circ as structural Verilog: 1 circuit, main circuit main
// 8
module main (
  input  [7:0] AB,
  input  PEGA_PC,
  input  LDA,
  input  STA
);

  wire and_2_out, and_3_out, clock_1_out, demultiplexer_2_out1, demultiplexer_2_out3, LDA_t, not_1_out,
       PC_plus_plus, Pega, Pega_PC_t, STA_t, stop;
  wire [0:0] and_1_out;
  wire [1:0] counter_1_q;
  wire [7:0] AB_t, \Endereço , \Instrução , JMP, PC;
  wire [15:0] Acc, ram_1_data, setAcc, setIR, Valor;

  Clock clock_1 (.out(clock_1_out));
  Register #(.width(16)) IR (.D(setIR), .en(Pega_PC_t), .Q({\Instrução , AB_t}), .clk(clock_1_out), .clr(1'b0));
  not not_1 (not_1_out, Pega_PC_t);
  or or_1 (Pega, Pega_PC_t, LDA_t);
  Multiplexer #(.select(2), .width(8), .enable("false")) multiplexer_1 (
    .in0(PC), .in1(AB_t), .in2(AB_t), .out(\Endereço ), .sel({STA_t, and_1_out[0]}));  // open: in3
  and and_1 (and_1_out[0], LDA_t, not_1_out);
  Demultiplexer #(.width(16), .enable("false")) demultiplexer_1 (
    .out0(setIR), .out1(setAcc), .in(Valor), .sel(and_1_out[0]));
  Register #(.width(16)) Acumulador (.D(setAcc), .en(LDA_t), .Q(Acc), .clk(clock_1_out), .clr(1'b0));
  and and_2 (and_2_out, clock_1_out, STA_t);
  Counter #(.width(2), .max('h2)) counter_1 (.Q(counter_1_q), .clk(and_3_out));  // open: load, D, count, carry, clr
  and and_3 (and_3_out, clock_1_out, ~stop);  // AND_Gate
  Demultiplexer #(.select(2), .enable("false")) demultiplexer_2 (
    .out0(Pega_PC_t), .out1(demultiplexer_2_out1), .out2(PC_plus_plus), .out3(demultiplexer_2_out3),
    .in(1'b1), .sel(counter_1_q));
  IF_main main_1 (
    .out_3(LDA_t), .STA(STA_t), .out_5(stop), .in_1(\Instrução ), .in_2(demultiplexer_2_out1));  // open: out_6, out_7
  RAM #(.dataWidth(16)) ram_1 (
    .addr(\Endereço ), .data(ram_1_data), .sel(1'b1), .clk(and_2_out), .ld(Pega), .clr(1'b0));
  Transistor #(.\type ("n"), .width(16)) transistor_1 (.in(Acc), .out(ram_1_data), .gate(STA_t));
  Transistor #(.\type ("n"), .width(16)) transistor_2 (.in(ram_1_data), .out(Valor), .gate(Pega));
  PC_main main_2 (.in_1(PC_plus_plus), .out_4(PC), .in_3(JMP));  // open: in_2
endmodule
