// Logisim project IF.circ as structural Verilog: 1 circuit, main circuit main
module main (
  input  [7:0] in_1,
  input  in_2,
  output out_3,
  output STA,
  output out_5,
  output out_6,
  output out_7
);

  wire and_3_out, and_4_out, and_7_out, and_8_out, and_10_out;

  and and_1 (out_3, in_2, and_4_out);
  and and_2 (out_6, in_2, and_3_out);
  and and_3 (and_3_out, ~in_1[0], in_1[1], ~in_1[2], ~in_1[3], in_1[4], in_1[5], ~in_1[6], ~in_1[7]);  // AND_Gate
  and and_4 (and_4_out, in_1[0], in_1[1], ~in_1[2], in_1[3], ~in_1[4], ~in_1[5], ~in_1[6], ~in_1[7]);  // AND_Gate
  and and_5 (STA, in_2, and_7_out);
  and and_6 (out_7, in_2, and_8_out);
  and and_7 (and_7_out, ~in_1[0], ~in_1[1], in_1[2], in_1[3], ~in_1[4], ~in_1[5], ~in_1[6], ~in_1[7]);  // AND_Gate
  and and_8 (and_8_out, in_1[0], ~in_1[1], ~in_1[2], ~in_1[3], in_1[4], in_1[5], ~in_1[6], ~in_1[7]);  // AND_Gate
  and and_9 (out_5, in_2, and_10_out);
  and and_10 (and_10_out, ~in_1[0], in_1[1], in_1[2], ~in_1[3], ~in_1[4], ~in_1[5], in_1[6], ~in_1[7]);  // AND_Gate

  // Other names for the same wires on the sheet: Enable = in_2; _0 = in_1[0]; _1 = in_1[1]; _2 = in_1[2];
  //   _3 = in_1[3]; _4 = in_1[4]; _5 = in_1[5]; _6 = in_1[6]; _7 = in_1[7]

  // Notes on the sheet:
  //   Load
  //   NOP
  //   JMP
  //   STP
endmodule
