// Logisim project IR.circ as structural Verilog: 1 circuit, main circuit main
module main (
  input  [15:0] in_1,
  input  in_2,
  output [15:0] out_3
);

  Register #(.width(16)) register_1 (.D(in_1), .en(1'b1), .Q(out_3), .clr(in_2));  // open: clk
endmodule
