// Logisim project PC.circ as structural Verilog: 1 circuit, main circuit main
module main (
  input  in_1,
  input  in_2,
  input  in_3,
  input  [7:0] in_4,
  output [7:0] out_5
);

  wire and_1_out, and_2_out, and_3_out, and_4_out, and_5_out, and_6_out, and_7_out, and_8_out, and_9_out,
       and_10_out, and_11_out, and_12_out, and_13_out, and_14_out, and_15_out, and_16_out, j_k_ff_1_qn,
       j_k_ff_2_qn, j_k_ff_3_qn, j_k_ff_4_qn, j_k_ff_5_qn, j_k_ff_6_qn, j_k_ff_7_qn, or_1_out, or_2_out,
       or_3_out, or_4_out, or_5_out, or_6_out, or_7_out, or_8_out;

  J_K_Flip_Flop j_k_ff_1 (
    .J(1'b1), .clk(in_1), .K(1'b1), .Q(out_5[0]), .Qn(j_k_ff_1_qn), .preset(and_2_out), .en(1'b1),
    .reset(or_1_out));
  or or_1 (or_1_out, in_2, and_3_out);
  and and_1 (and_1_out, in_3, in_4[1]);
  and and_2 (and_2_out, in_3, in_4[0]);
  and and_3 (and_3_out, in_3, ~in_4[0]);  // AND_Gate
  J_K_Flip_Flop j_k_ff_2 (
    .J(1'b1), .clk(j_k_ff_1_qn), .K(1'b1), .Q(out_5[1]), .Qn(j_k_ff_2_qn), .preset(and_1_out), .en(1'b1),
    .reset(or_2_out));
  or or_2 (or_2_out, in_2, and_4_out);
  and and_4 (and_4_out, in_3, ~in_4[1]);  // AND_Gate
  and and_5 (and_5_out, in_3, in_4[2]);
  J_K_Flip_Flop j_k_ff_3 (
    .J(1'b1), .clk(j_k_ff_2_qn), .K(1'b1), .Q(out_5[2]), .Qn(j_k_ff_3_qn), .preset(and_5_out), .en(1'b1),
    .reset(or_3_out));
  or or_3 (or_3_out, in_2, and_7_out);
  or or_4 (or_4_out, in_2, and_8_out);
  and and_6 (and_6_out, in_3, in_4[3]);
  and and_7 (and_7_out, in_3, ~in_4[2]);  // AND_Gate
  J_K_Flip_Flop j_k_ff_4 (
    .J(1'b1), .clk(j_k_ff_5_qn), .K(1'b1), .Q(out_5[4]), .Qn(j_k_ff_4_qn), .preset(and_9_out), .en(1'b1),
    .reset(or_5_out));
  J_K_Flip_Flop j_k_ff_5 (
    .J(1'b1), .clk(j_k_ff_3_qn), .K(1'b1), .Q(out_5[3]), .Qn(j_k_ff_5_qn), .preset(and_6_out), .en(1'b1),
    .reset(or_4_out));
  or or_5 (or_5_out, in_2, and_10_out);
  and and_8 (and_8_out, in_3, ~in_4[3]);  // AND_Gate
  and and_9 (and_9_out, in_3, in_4[4]);
  and and_10 (and_10_out, in_3, ~in_4[4]);  // AND_Gate
  J_K_Flip_Flop j_k_ff_6 (
    .J(1'b1), .clk(j_k_ff_4_qn), .K(1'b1), .Q(out_5[5]), .Qn(j_k_ff_6_qn), .preset(and_12_out), .en(1'b1),
    .reset(or_6_out));
  or or_6 (or_6_out, in_2, and_11_out);
  and and_11 (and_11_out, in_3, ~in_4[5]);  // AND_Gate
  and and_12 (and_12_out, in_3, in_4[5]);
  J_K_Flip_Flop j_k_ff_7 (
    .J(1'b1), .clk(j_k_ff_6_qn), .K(1'b1), .Q(out_5[6]), .Qn(j_k_ff_7_qn), .preset(and_14_out), .en(1'b1),
    .reset(or_7_out));
  or or_7 (or_7_out, in_2, and_13_out);
  and and_13 (and_13_out, in_3, ~in_4[6]);  // AND_Gate
  and and_14 (and_14_out, in_3, in_4[6]);
  J_K_Flip_Flop j_k_ff_8 (
    .J(1'b1), .clk(j_k_ff_7_qn), .K(1'b1), .Q(out_5[7]), .preset(and_16_out), .en(1'b1), .reset(or_8_out));  // open: Qn
  or or_8 (or_8_out, in_2, and_15_out);
  and and_15 (and_15_out, in_3, ~in_4[7]);  // AND_Gate
  and and_16 (and_16_out, in_3, in_4[7]);
endmodule
