// Logisim project controlador_compacto.circ as structural Verilog: 1 circuit, main circuit main
module main (
  input  CLOCK,
  input  RESET,
  input  [7:0] PC,
  input  [15:0] ACC_OUT,
  input  [15:0] IR_OUT,
  input  [15:0] RAM_OUT,
  output PC_plus_plus,
  output [15:0] ACC_IN,
  output [15:0] IR_IN,
  output [7:0] RAM_ADDR,
  output RAM_CLOCK,
  output READ_ENABLE,
  output PC_ENABLE,
  output ACC_ENABLE,
  output IR_ENABLE
);

  wire and_1_out, and_2_out, not_1_out, not_4_out, or_1_out, RAM_CLOCK_t, STA, STOP;
  wire [1:0] counter_1_q;
  wire [15:0] RAM_OUT_t;

  not not_1 (not_1_out, IR_ENABLE);
  Multiplexer #(.width(8), .enable("false")) multiplexer_1 (
    .in0(PC), .in1(IR_OUT[7:0]), .out(RAM_ADDR), .sel(or_1_out));
  or or_1 (or_1_out, STA, and_1_out);
  and and_1 (and_1_out, ACC_ENABLE, not_1_out);
  Demultiplexer #(.width(16), .enable("false")) demultiplexer_1 (
    .out0(IR_IN), .out1(ACC_IN), .in(RAM_OUT_t), .sel(and_1_out));
  not not_2 (RAM_CLOCK, RAM_CLOCK_t);
  not not_3 (READ_ENABLE, STA);
  Counter #(.width(2), .max('h2)) counter_1 (
    .Q(counter_1_q), .clk(and_2_out), .clr(RESET));  // open: load, D, count, carry
  and and_2 (and_2_out, CLOCK, ~STOP);  // AND_Gate
  Transistor #(.\type ("n"), .width(16)) transistor_1 (.in(ACC_OUT), .out(RAM_OUT), .gate(STA));
  not not_4 (not_4_out, STA);
  Demultiplexer #(.select(2), .enable("false")) demultiplexer_2 (
    .out0(IR_ENABLE), .out1(RAM_CLOCK_t), .out2(PC_plus_plus), .in(1'b1), .sel(counter_1_q));  // open: out3
  Transistor #(.\type ("n"), .width(16)) transistor_2 (.in(RAM_OUT), .out(RAM_OUT_t), .gate(not_4_out));
  IF_main main_1 (
    .out_3(ACC_ENABLE), .out_7(PC_ENABLE), .STA(STA), .out_5(STOP), .in_1(IR_OUT[15:8]), .in_2(RAM_CLOCK_t));  // open: out_6

  // Other names for the same wires on the sheet: IR_ADDR[7:0] = IR_OUT[7:0]; IR_INST[7:0] = IR_OUT[15:8];
  //   JMP = PC_ENABLE; LDA = ACC_ENABLE; PEGA_PC = IR_ENABLE; RAM_I_O[15:0] = RAM_OUT
endmodule
