// Logisim project AnalisaAcumulador.circ as structural Verilog: 1 circuit, main circuit main
module main (
  input  [15:0] in_1,
  output _0,
  output out_3,
  output _0_2,
  output out_5,
  output _0_3,
  output _0_4
);

  wire or_2_out, or_4_out;

  or or_1 (out_5, in_1[15], _0_4);
  not not_1 (_0_3, _0_4);
  and and_1 (_0_4, ~or_2_out, ~in_1[15]);  // AND_Gate
  or or_2 (or_2_out, in_1[0], in_1[1], in_1[2], in_1[3], in_1[4], in_1[5], in_1[6], in_1[7], in_1[8], in_1[9], in_1[10], in_1[11], in_1[12], in_1[13], in_1[14]);
  or or_3 (_0, _0_4, out_3);
  or or_4 (or_4_out, in_1[0], in_1[1], in_1[2], in_1[3], in_1[4], in_1[5], in_1[6], in_1[7], in_1[8], in_1[9], in_1[10], in_1[11], in_1[12], in_1[13], in_1[14]);
  and and_2 (out_3, or_4_out, ~in_1[15]);  // AND_Gate

  assign _0_2 = in_1[15];

  // Other names for the same wires on the sheet: _0_14[14:0] = in_1[14:0]; _15 = in_1[15]

  // Notes on the sheet:
  //   <= 0
  //   > 0
endmodule
