// Logisim project Jumpador.circ as structural Verilog: 1 circuit, main circuit main
module main (
  input  JMP,
  input  JLE,
  input  JDZ,
  input  JGT,
  input  JEQ,
  input  JLT,
  input  JGE,
  input  [15:0] in_8,
  output PC_ENABLE
);

  wire and_1_out, and_2_out, and_3_out, and_4_out, and_5_out, and_6_out, and_7_out, and_8_out, not_1_out,
       or_1_out, or_2_out, or_3_out, or_4_out;

  or or_1 (or_1_out, in_8[15], and_1_out);
  not not_1 (not_1_out, and_1_out);
  or or_2 (or_2_out, in_8[0], in_8[1], in_8[2], in_8[3], in_8[4], in_8[5], in_8[6], in_8[7], in_8[8], in_8[9], in_8[10], in_8[11], in_8[12], in_8[13], in_8[14]);
  or or_3 (or_3_out, and_1_out, and_2_out);
  and and_1 (and_1_out, ~or_2_out, ~in_8[15]);  // AND_Gate
  and and_2 (and_2_out, or_4_out, ~in_8[15]);  // AND_Gate
  or or_4 (or_4_out, in_8[0], in_8[1], in_8[2], in_8[3], in_8[4], in_8[5], in_8[6], in_8[7], in_8[8], in_8[9], in_8[10], in_8[11], in_8[12], in_8[13], in_8[14]);
  and and_3 (and_3_out, JLE, or_1_out);
  and and_4 (and_4_out, JDZ, not_1_out);
  and and_5 (and_5_out, JGT, and_2_out);
  and and_6 (and_6_out, JEQ, and_1_out);
  and and_7 (and_7_out, JLT, in_8[15]);
  and and_8 (and_8_out, JGE, or_3_out);
  or or_5 (PC_ENABLE, JMP, and_3_out, and_4_out, and_5_out, and_6_out, and_7_out, and_8_out);

  // Other names for the same wires on the sheet: _0_14[14:0] = in_8[14:0]; _15 = in_8[15]
endmodule
