// Logisim project ifzaozao.circ as structural Verilog: 1 circuit, main circuit main
module main (
  input  [7:0] in_1,
  input  in_2,
  output out_3,
  output out_4,
  output out_5,
  output out_6,
  output out_7,
  output out_8,
  output out_9,
  output out_10,
  output out_11,
  output out_12,
  output out_13,
  output out_14,
  output out_15,
  output out_16,
  output out_17,
  output out_18,
  output out_19,
  output STA
);

  wire and_6_out, and_7_out, and_8_out, and_13_out, and_14_out, and_15_out, and_16_out, and_21_out,
       and_22_out, and_23_out, and_24_out, and_29_out, and_30_out, and_31_out, and_32_out, and_35_out,
       and_36_out, undriven;

  and and_1 (out_3, in_2, and_8_out);
  and and_2 (out_9, in_2, undriven);
  and and_3 (out_16, in_2, and_6_out);
  and and_4 (out_17, in_2, and_7_out);
  // AND_Gate and_5 has open pins: in0=in_1[0], in1=in_1[1], in2=in_1[2], in3=in_1[3], in4=in_1[4], in5=in_1[5], in6=in_1[6], in7=in_1[7], out=open
  and and_6 (and_6_out, in_1[0], in_1[1], in_1[2], ~in_1[3], in_1[4], ~in_1[5], ~in_1[6], ~in_1[7]);  // AND_Gate
  and and_7 (and_7_out, ~in_1[0], ~in_1[1], ~in_1[2], in_1[3], in_1[4], ~in_1[5], ~in_1[6], ~in_1[7]);  // AND_Gate
  and and_8 (and_8_out, in_1[0], ~in_1[1], in_1[2], ~in_1[3], in_1[4], ~in_1[5], ~in_1[6], ~in_1[7]);  // AND_Gate
  and and_9 (out_4, in_2, and_15_out);
  and and_10 (out_8, in_2, and_16_out);
  and and_11 (out_14, in_2, and_13_out);
  and and_12 (out_18, in_2, and_14_out);
  and and_13 (and_13_out, in_1[0], ~in_1[1], in_1[2], ~in_1[3], in_1[4], in_1[5], ~in_1[6], ~in_1[7]);  // AND_Gate
  and and_14 (and_14_out, ~in_1[0], in_1[1], in_1[2], ~in_1[3], in_1[4], in_1[5], ~in_1[6], ~in_1[7]);  // AND_Gate
  and and_15 (and_15_out, in_1[0], ~in_1[1], ~in_1[2], in_1[3], in_1[4], ~in_1[5], ~in_1[6], ~in_1[7]);  // AND_Gate
  and and_16 (and_16_out, ~in_1[0], ~in_1[1], in_1[2], ~in_1[3], in_1[4], in_1[5], ~in_1[6], ~in_1[7]);  // AND_Gate
  and and_17 (out_5, in_2, and_21_out);
  and and_18 (out_10, in_2, and_22_out);
  and and_19 (out_13, in_2, and_23_out);
  and and_20 (out_19, in_2, and_24_out);
  and and_21 (and_21_out, in_1[0], in_1[1], in_1[2], ~in_1[3], in_1[4], in_1[5], ~in_1[6], ~in_1[7]);  // AND_Gate
  and and_22 (and_22_out, ~in_1[0], ~in_1[1], ~in_1[2], in_1[3], in_1[4], in_1[5], ~in_1[6], ~in_1[7]);  // AND_Gate
  and and_23 (and_23_out, in_1[0], ~in_1[1], ~in_1[2], in_1[3], in_1[4], in_1[5], ~in_1[6], ~in_1[7]);  // AND_Gate
  and and_24 (and_24_out, in_1[0], in_1[1], in_1[2], in_1[3], in_1[4], ~in_1[5], ~in_1[6], ~in_1[7]);  // AND_Gate
  and and_25 (out_6, in_2, and_29_out);
  and and_26 (out_11, in_2, and_30_out);
  and and_27 (out_15, in_2, and_31_out);
  and and_28 (STA, in_2, and_32_out);
  and and_29 (and_29_out, in_1[0], ~in_1[1], ~in_1[2], in_1[3], ~in_1[4], in_1[5], ~in_1[6], ~in_1[7]);  // AND_Gate
  and and_30 (and_30_out, in_1[0], in_1[1], ~in_1[2], in_1[3], ~in_1[4], ~in_1[5], ~in_1[6], ~in_1[7]);  // AND_Gate
  and and_31 (and_31_out, ~in_1[0], in_1[1], ~in_1[2], ~in_1[3], in_1[4], in_1[5], ~in_1[6], ~in_1[7]);  // AND_Gate
  and and_32 (and_32_out, ~in_1[0], ~in_1[1], in_1[2], in_1[3], ~in_1[4], ~in_1[5], ~in_1[6], ~in_1[7]);  // AND_Gate
  and and_33 (out_7, in_2, and_35_out);
  and and_34 (out_12, in_2, and_36_out);
  and and_35 (and_35_out, in_1[0], in_1[1], ~in_1[2], ~in_1[3], in_1[4], in_1[5], ~in_1[6], ~in_1[7]);  // AND_Gate
  and and_36 (and_36_out, ~in_1[0], in_1[1], in_1[2], ~in_1[3], ~in_1[4], ~in_1[5], in_1[6], ~in_1[7]);  // AND_Gate

  // Other names for the same wires on the sheet: Enable = in_2; _0 = in_1[0]; _1 = in_1[1]; _2 = in_1[2];
  //   _3 = in_1[3]; _4 = in_1[4]; _5 = in_1[5]; _6 = in_1[6]; _7 = in_1[7]

  // Notes on the sheet:
  //   ADD
  //   SUB
  //   MUL
  //   DIV
  //   JDZ
  //   REM
  //   JLE
  //   JGT
  //   JEQ
  //   JLT
  //   JGE
  //   INN
  //   PRN
  //   Load
  //   NOP
  //   JMP
  //   STP
endmodule
