// Logisim project tradutor.circ as structural Verilog: 1 circuit, main circuit main
module main (
  input  [7:0] in_1,
  output [2:0] out_2
);

  wire and_2_out, and_3_out, not_1_out, not_2_out, not_3_out;

  and and_1 (out_2[2], in_1[0], not_1_out);
  not not_1 (not_1_out, in_1[2]);
  not not_2 (not_2_out, in_1[0]);
  not not_3 (not_3_out, in_1[2]);
  and and_2 (and_2_out, not_3_out, not_2_out);
  or or_1 (out_2[1], and_2_out, and_3_out);
  and and_3 (and_3_out, in_1[1], in_1[0]);
  not not_4 (out_2[0], in_1[0]);

  // Other names for the same wires on the sheet: C = in_1[0]; B = in_1[1]; A = in_1[2]; Z = out_2[0]; Y = out_2[1];
  //   X = out_2[2]
endmodule
