// Logisim project somaSecondTRy.circ as structural Verilog: 3 circuits, main circuit main
module soma (
  input  carry_in,
  input  X,
  input  in_3,
  input  in_4,
  input  in_5,
  input  in_6,
  input  in_7,
  input  in_8,
  input  in_9,
  input  Y,
  input  in_11,
  input  in_12,
  input  in_13,
  input  in_14,
  input  in_15,
  input  in_16,
  input  in_17,
  output out_18,
  output out_19,
  output out_20,
  output out_21,
  output out_22,
  output out_23,
  output out_24,
  output Z,
  output out_26
);

  wire and_1_out, and_2_out, and_3_out, and_4_out, and_5_out, and_6_out, and_7_out, and_8_out, and_9_out,
       and_10_out, and_11_out, and_12_out, and_13_out, and_14_out, and_15_out, and_16_out, or_1_out,
       or_2_out, or_3_out, or_4_out, or_5_out, or_6_out, or_7_out, xor_1_out, xor_3_out, xor_5_out,
       xor_7_out, xor_9_out, xor_11_out, xor_13_out, xor_15_out;

  xor xor_1 (xor_1_out, X, Y);
  xor xor_2 (Z, xor_1_out, carry_in);
  and and_1 (and_1_out, Y, X);
  or or_1 (or_1_out, and_1_out, and_2_out);
  and and_2 (and_2_out, xor_1_out, carry_in);
  xor xor_3 (xor_3_out, in_3, in_11);
  xor xor_4 (out_18, xor_3_out, or_1_out);
  and and_3 (and_3_out, in_11, in_3);
  and and_4 (and_4_out, or_1_out, xor_3_out);
  or or_2 (or_2_out, and_3_out, and_4_out);
  xor xor_5 (xor_5_out, in_4, in_12);
  xor xor_6 (out_19, xor_5_out, or_2_out);
  and and_5 (and_5_out, in_12, in_4);
  and and_6 (and_6_out, or_2_out, xor_5_out);
  or or_3 (or_3_out, and_5_out, and_6_out);
  xor xor_7 (xor_7_out, in_5, in_13);
  xor xor_8 (out_20, xor_7_out, or_3_out);
  and and_7 (and_7_out, in_13, in_5);
  and and_8 (and_8_out, or_3_out, xor_7_out);
  or or_4 (or_4_out, and_7_out, and_8_out);
  xor xor_9 (xor_9_out, in_6, in_14);
  xor xor_10 (out_21, xor_9_out, or_4_out);
  and and_9 (and_9_out, in_14, in_6);
  and and_10 (and_10_out, or_4_out, xor_9_out);
  or or_5 (or_5_out, and_9_out, and_10_out);
  xor xor_11 (xor_11_out, in_7, in_15);
  xor xor_12 (out_22, xor_11_out, or_5_out);
  and and_11 (and_11_out, in_15, in_7);
  or or_6 (or_6_out, and_11_out, and_12_out);
  and and_12 (and_12_out, or_5_out, xor_11_out);
  xor xor_13 (xor_13_out, in_8, in_16);
  xor xor_14 (out_23, xor_13_out, or_6_out);
  and and_13 (and_13_out, in_16, in_8);
  and and_14 (and_14_out, or_6_out, xor_13_out);
  or or_7 (or_7_out, and_13_out, and_14_out);
  xor xor_15 (xor_15_out, in_9, in_17);
  xor xor_16 (out_24, xor_15_out, or_7_out);
  and and_15 (and_15_out, in_17, in_9);
  and and_16 (and_16_out, or_7_out, xor_15_out);
  or or_8 (out_26, and_15_out, and_16_out);

  // Notes on the sheet:
  //   in_13: pull=down
  //   in_17: pull=down
  //   in_15: pull=down
  //   in_12: pull=down
  //   in_11: pull=down
  //   in_16: pull=down
  //   Y: pull=down
  //   in_14: pull=down
  //   carry out
  //   carry out
  //   carry out
  //   carry out
  //   carry out
  //   carry out
  //   carry out
  //   overflow
  //   carry out
endmodule

module main (
  input  in_1,
  input  in_2,
  input  in_3,
  input  in_4,
  input  in_5,
  input  in_6,
  input  in_7,
  input  in_8,
  input  in_9,
  input  in_10,
  input  in_11,
  input  in_12,
  input  in_13,
  input  in_14,
  input  in_15,
  input  in_16,
  output out_17,
  output out_18,
  output out_19,
  output out_20,
  output out_21,
  output out_22,
  output out_23,
  output out_24,
  output out_25
);

  wire auxiliar_1_out_10, auxiliar_1_out_11, auxiliar_1_out_12, auxiliar_1_out_13, auxiliar_1_out_14,
       auxiliar_1_out_15, auxiliar_1_out_16, auxiliar_1_out_17, auxiliar_2_out_10, auxiliar_2_out_11,
       auxiliar_2_out_12, auxiliar_2_out_13, auxiliar_2_out_14, auxiliar_2_out_15, auxiliar_2_out_16,
       auxiliar_2_out_17, auxiliar_3_out_10, auxiliar_3_out_11, auxiliar_3_out_12, auxiliar_3_out_13,
       auxiliar_3_out_14, auxiliar_3_out_15, auxiliar_3_out_16, auxiliar_3_out_17, auxiliar_4_out_10,
       auxiliar_4_out_11, auxiliar_4_out_12, auxiliar_4_out_13, auxiliar_4_out_14, auxiliar_4_out_15,
       auxiliar_4_out_16, auxiliar_4_out_17, auxiliar_5_out_10, auxiliar_5_out_11, auxiliar_5_out_12,
       auxiliar_5_out_13, auxiliar_5_out_14, auxiliar_5_out_15, auxiliar_5_out_16, auxiliar_5_out_17,
       auxiliar_6_out_10, auxiliar_6_out_11, auxiliar_6_out_12, auxiliar_6_out_13, auxiliar_6_out_14,
       auxiliar_6_out_15, auxiliar_6_out_16, auxiliar_6_out_17, auxiliar_7_out_10, auxiliar_7_out_11,
       auxiliar_7_out_12, auxiliar_7_out_13, auxiliar_7_out_14, auxiliar_7_out_15, auxiliar_7_out_16,
       auxiliar_7_out_17, auxiliar_8_out_10, auxiliar_8_out_11, auxiliar_8_out_12, auxiliar_8_out_13,
       auxiliar_8_out_14, auxiliar_8_out_15, auxiliar_8_out_16, auxiliar_8_out_17, C0, C1, C2, C3, C4, C5,
       C6, soma_1_out_18, soma_1_out_19, soma_1_out_20, soma_1_out_21, soma_1_out_22, soma_1_out_23,
       soma_1_out_24, soma_2_out_18, soma_2_out_19, soma_2_out_20, soma_2_out_21, soma_2_out_22,
       soma_2_out_23, soma_2_out_24, soma_3_out_18, soma_3_out_19, soma_3_out_20, soma_3_out_21,
       soma_3_out_22, soma_3_out_23, soma_3_out_24, soma_3_out_26, soma_4_out_18, soma_4_out_19,
       soma_4_out_20, soma_4_out_21, soma_4_out_22, soma_4_out_23, soma_4_out_24, soma_5_out_18,
       soma_5_out_19, soma_5_out_20, soma_5_out_21, soma_5_out_22, soma_5_out_23, soma_5_out_24,
       soma_6_out_18, soma_6_out_19, soma_6_out_20, soma_6_out_21, soma_6_out_22, soma_6_out_23,
       soma_6_out_24, soma_7_out_18, soma_7_out_19, soma_7_out_20, soma_7_out_21, soma_7_out_22,
       soma_7_out_23, soma_7_out_24, soma_8_out_18, soma_8_out_19, soma_8_out_20, soma_8_out_21,
       soma_8_out_22, soma_8_out_23, soma_8_out_24;

  soma soma_1 (
    .X(soma_8_out_18), .Y(auxiliar_7_out_10), .in_3(soma_8_out_19), .in_11(auxiliar_7_out_11),
    .in_4(soma_8_out_20), .in_12(auxiliar_7_out_12), .in_5(soma_8_out_21), .in_13(auxiliar_7_out_13),
    .in_6(soma_8_out_22), .in_14(auxiliar_7_out_14), .in_7(soma_8_out_23), .in_15(auxiliar_7_out_15),
    .in_8(soma_8_out_24), .in_16(auxiliar_7_out_16), .in_9(C4), .in_17(auxiliar_7_out_17), .Z(out_23),
    .out_18(soma_1_out_18), .out_19(soma_1_out_19), .out_20(soma_1_out_20), .out_21(soma_1_out_21),
    .out_22(soma_1_out_22), .out_23(soma_1_out_23), .out_24(soma_1_out_24), .out_26(C5), .carry_in(1'b0));
  soma soma_2 (
    .X(soma_1_out_18), .Y(auxiliar_8_out_10), .in_3(soma_1_out_19), .in_11(auxiliar_8_out_11),
    .in_4(soma_1_out_20), .in_12(auxiliar_8_out_12), .in_5(soma_1_out_21), .in_13(auxiliar_8_out_13),
    .in_6(soma_1_out_22), .in_14(auxiliar_8_out_14), .in_7(soma_1_out_23), .in_15(auxiliar_8_out_15),
    .in_8(soma_1_out_24), .in_16(auxiliar_8_out_16), .in_9(C5), .in_17(auxiliar_8_out_17), .Z(out_24),
    .out_18(soma_2_out_18), .out_19(soma_2_out_19), .out_20(soma_2_out_20), .out_21(soma_2_out_21),
    .out_22(soma_2_out_22), .out_23(soma_2_out_23), .out_24(soma_2_out_24), .out_26(C6), .carry_in(1'b0));
  soma soma_3 (
    .X(soma_2_out_18), .Y(auxiliar_1_out_10), .in_3(soma_2_out_19), .in_11(auxiliar_1_out_11),
    .in_4(soma_2_out_20), .in_12(auxiliar_1_out_12), .in_5(soma_2_out_21), .in_13(auxiliar_1_out_13),
    .in_6(soma_2_out_22), .in_14(auxiliar_1_out_14), .in_7(soma_2_out_23), .in_15(auxiliar_1_out_15),
    .in_8(soma_2_out_24), .in_16(auxiliar_1_out_16), .in_9(C6), .in_17(auxiliar_1_out_17), .Z(out_25),
    .out_18(soma_3_out_18), .out_19(soma_3_out_19), .out_20(soma_3_out_20), .out_21(soma_3_out_21),
    .out_22(soma_3_out_22), .out_23(soma_3_out_23), .out_24(soma_3_out_24), .out_26(soma_3_out_26),
    .carry_in(1'b0));
  soma soma_4 (
    .X(1'b0), .Y(auxiliar_2_out_10), .in_3(1'b0), .in_11(auxiliar_2_out_11), .in_4(1'b0),
    .in_12(auxiliar_2_out_12), .in_5(1'b0), .in_13(auxiliar_2_out_13), .in_6(1'b0),
    .in_14(auxiliar_2_out_14), .in_7(1'b0), .in_15(auxiliar_2_out_15), .in_8(1'b0),
    .in_16(auxiliar_2_out_16), .in_9(1'b0), .in_17(auxiliar_2_out_17), .Z(out_18), .out_18(soma_4_out_18),
    .out_19(soma_4_out_19), .out_20(soma_4_out_20), .out_21(soma_4_out_21), .out_22(soma_4_out_22),
    .out_23(soma_4_out_23), .out_24(soma_4_out_24), .out_26(C0), .carry_in(1'b0));
  soma soma_5 (
    .X(soma_4_out_18), .Y(auxiliar_3_out_10), .in_3(soma_4_out_19), .in_11(auxiliar_3_out_11),
    .in_4(soma_4_out_20), .in_12(auxiliar_3_out_12), .in_5(soma_4_out_21), .in_13(auxiliar_3_out_13),
    .in_6(soma_4_out_22), .in_14(auxiliar_3_out_14), .in_7(soma_4_out_23), .in_15(auxiliar_3_out_15),
    .in_8(soma_4_out_24), .in_16(auxiliar_3_out_16), .in_9(C0), .in_17(auxiliar_3_out_17), .Z(out_19),
    .out_18(soma_5_out_18), .out_19(soma_5_out_19), .out_20(soma_5_out_20), .out_21(soma_5_out_21),
    .out_22(soma_5_out_22), .out_23(soma_5_out_23), .out_24(soma_5_out_24), .out_26(C1), .carry_in(1'b0));
  soma soma_6 (
    .X(soma_5_out_18), .Y(auxiliar_4_out_10), .in_3(soma_5_out_19), .in_11(auxiliar_4_out_11),
    .in_4(soma_5_out_20), .in_12(auxiliar_4_out_12), .in_5(soma_5_out_21), .in_13(auxiliar_4_out_13),
    .in_6(soma_5_out_22), .in_14(auxiliar_4_out_14), .in_7(soma_5_out_23), .in_15(auxiliar_4_out_15),
    .in_8(soma_5_out_24), .in_16(auxiliar_4_out_16), .in_9(C1), .in_17(auxiliar_4_out_17), .Z(out_20),
    .out_18(soma_6_out_18), .out_19(soma_6_out_19), .out_20(soma_6_out_20), .out_21(soma_6_out_21),
    .out_22(soma_6_out_22), .out_23(soma_6_out_23), .out_24(soma_6_out_24), .out_26(C2), .carry_in(1'b0));
  soma soma_7 (
    .X(soma_6_out_18), .Y(auxiliar_5_out_10), .in_3(soma_6_out_19), .in_11(auxiliar_5_out_11),
    .in_4(soma_6_out_20), .in_12(auxiliar_5_out_12), .in_5(soma_6_out_21), .in_13(auxiliar_5_out_13),
    .in_6(soma_6_out_22), .in_14(auxiliar_5_out_14), .in_7(soma_6_out_23), .in_15(auxiliar_5_out_15),
    .in_8(soma_6_out_24), .in_16(auxiliar_5_out_16), .in_9(C2), .in_17(auxiliar_5_out_17), .Z(out_21),
    .out_18(soma_7_out_18), .out_19(soma_7_out_19), .out_20(soma_7_out_20), .out_21(soma_7_out_21),
    .out_22(soma_7_out_22), .out_23(soma_7_out_23), .out_24(soma_7_out_24), .out_26(C3), .carry_in(1'b0));
  soma soma_8 (
    .X(soma_7_out_18), .Y(auxiliar_6_out_10), .in_3(soma_7_out_19), .in_11(auxiliar_6_out_11),
    .in_4(soma_7_out_20), .in_12(auxiliar_6_out_12), .in_5(soma_7_out_21), .in_13(auxiliar_6_out_13),
    .in_6(soma_7_out_22), .in_14(auxiliar_6_out_14), .in_7(soma_7_out_23), .in_15(auxiliar_6_out_15),
    .in_8(soma_7_out_24), .in_16(auxiliar_6_out_16), .in_9(C3), .in_17(auxiliar_6_out_17), .Z(out_22),
    .out_18(soma_8_out_18), .out_19(soma_8_out_19), .out_20(soma_8_out_20), .out_21(soma_8_out_21),
    .out_22(soma_8_out_22), .out_23(soma_8_out_23), .out_24(soma_8_out_24), .out_26(C4), .carry_in(1'b0));
  auxiliar auxiliar_1 (
    .in_9(in_16), .in_1(in_1), .in_2(in_2), .in_3(in_3), .in_4(in_4), .in_5(in_5), .in_6(in_6), .in_7(in_7),
    .in_8(in_8), .out_10(auxiliar_1_out_10), .out_11(auxiliar_1_out_11), .out_12(auxiliar_1_out_12),
    .out_13(auxiliar_1_out_13), .out_14(auxiliar_1_out_14), .out_15(auxiliar_1_out_15),
    .out_16(auxiliar_1_out_16), .out_17(auxiliar_1_out_17));
  or or_1 (out_17, soma_3_out_24, soma_3_out_23, soma_3_out_22, soma_3_out_21, soma_3_out_20, soma_3_out_19, soma_3_out_18, soma_3_out_26);
  auxiliar auxiliar_2 (
    .in_9(in_9), .in_1(in_1), .in_2(in_2), .in_3(in_3), .in_4(in_4), .in_5(in_5), .in_6(in_6), .in_7(in_7),
    .in_8(in_8), .out_10(auxiliar_2_out_10), .out_11(auxiliar_2_out_11), .out_12(auxiliar_2_out_12),
    .out_13(auxiliar_2_out_13), .out_14(auxiliar_2_out_14), .out_15(auxiliar_2_out_15),
    .out_16(auxiliar_2_out_16), .out_17(auxiliar_2_out_17));
  auxiliar auxiliar_3 (
    .in_9(in_10), .in_1(in_1), .in_2(in_2), .in_3(in_3), .in_4(in_4), .in_5(in_5), .in_6(in_6), .in_7(in_7),
    .in_8(in_8), .out_10(auxiliar_3_out_10), .out_11(auxiliar_3_out_11), .out_12(auxiliar_3_out_12),
    .out_13(auxiliar_3_out_13), .out_14(auxiliar_3_out_14), .out_15(auxiliar_3_out_15),
    .out_16(auxiliar_3_out_16), .out_17(auxiliar_3_out_17));
  auxiliar auxiliar_4 (
    .in_9(in_11), .in_1(in_1), .in_2(in_2), .in_3(in_3), .in_4(in_4), .in_5(in_5), .in_6(in_6), .in_7(in_7),
    .in_8(in_8), .out_10(auxiliar_4_out_10), .out_11(auxiliar_4_out_11), .out_12(auxiliar_4_out_12),
    .out_13(auxiliar_4_out_13), .out_14(auxiliar_4_out_14), .out_15(auxiliar_4_out_15),
    .out_16(auxiliar_4_out_16), .out_17(auxiliar_4_out_17));
  auxiliar auxiliar_5 (
    .in_9(in_12), .in_1(in_1), .in_2(in_2), .in_3(in_3), .in_4(in_4), .in_5(in_5), .in_6(in_6), .in_7(in_7),
    .in_8(in_8), .out_10(auxiliar_5_out_10), .out_11(auxiliar_5_out_11), .out_12(auxiliar_5_out_12),
    .out_13(auxiliar_5_out_13), .out_14(auxiliar_5_out_14), .out_15(auxiliar_5_out_15),
    .out_16(auxiliar_5_out_16), .out_17(auxiliar_5_out_17));
  auxiliar auxiliar_6 (
    .in_9(in_13), .in_1(in_1), .in_2(in_2), .in_3(in_3), .in_4(in_4), .in_5(in_5), .in_6(in_6), .in_7(in_7),
    .in_8(in_8), .out_10(auxiliar_6_out_10), .out_11(auxiliar_6_out_11), .out_12(auxiliar_6_out_12),
    .out_13(auxiliar_6_out_13), .out_14(auxiliar_6_out_14), .out_15(auxiliar_6_out_15),
    .out_16(auxiliar_6_out_16), .out_17(auxiliar_6_out_17));
  auxiliar auxiliar_7 (
    .in_9(in_14), .in_1(in_1), .in_2(in_2), .in_3(in_3), .in_4(in_4), .in_5(in_5), .in_6(in_6), .in_7(in_7),
    .in_8(in_8), .out_10(auxiliar_7_out_10), .out_11(auxiliar_7_out_11), .out_12(auxiliar_7_out_12),
    .out_13(auxiliar_7_out_13), .out_14(auxiliar_7_out_14), .out_15(auxiliar_7_out_15),
    .out_16(auxiliar_7_out_16), .out_17(auxiliar_7_out_17));
  auxiliar auxiliar_8 (
    .in_9(in_15), .in_1(in_1), .in_2(in_2), .in_3(in_3), .in_4(in_4), .in_5(in_5), .in_6(in_6), .in_7(in_7),
    .in_8(in_8), .out_10(auxiliar_8_out_10), .out_11(auxiliar_8_out_11), .out_12(auxiliar_8_out_12),
    .out_13(auxiliar_8_out_13), .out_14(auxiliar_8_out_14), .out_15(auxiliar_8_out_15),
    .out_16(auxiliar_8_out_16), .out_17(auxiliar_8_out_17));

  // Other names for the same wires on the sheet: _0 = in_1; _1 = in_2; _2 = in_3; _3 = in_4; _4 = in_5; _5 = in_6;
  //   _6 = in_7; _7 = in_8; E0 = in_9; E1 = in_10; E2 = in_11; E3 = in_12; E4 = in_13; E5 = in_14; E6 = in_15;
  //   E7 = in_16; OVERFLOW = out_17; S0 = out_18; S1 = out_19; S2 = out_20; S3 = out_21; S4 = out_22; S5 = out_23;
  //   S6 = out_24; S7 = out_25
endmodule

module auxiliar (
  input  in_1,
  input  in_2,
  input  in_3,
  input  in_4,
  input  in_5,
  input  in_6,
  input  in_7,
  input  in_8,
  input  in_9,
  output out_10,
  output out_11,
  output out_12,
  output out_13,
  output out_14,
  output out_15,
  output out_16,
  output out_17
);

  and and_1 (out_10, in_1, in_9);
  and and_2 (out_11, in_2, in_9);
  and and_3 (out_12, in_3, in_9);
  and and_4 (out_14, in_5, in_9);
  and and_5 (out_13, in_4, in_9);
  and and_6 (out_15, in_6, in_9);
  and and_7 (out_16, in_7, in_9);
  and and_8 (out_17, in_8, in_9);
endmodule
