// Logisim project somador-cloker.circ as structural Verilog: 3 circuits, main circuit main
module main (
  input  in_1,
  input  in_2,
  input  in_3,
  input  in_4,
  input  in_5,
  input  in_6,
  input  in_7,
  input  in_8,
  input  in_9,
  input  in_10,
  input  in_11,
  input  in_12,
  input  in_13,
  input  in_14,
  input  in_15,
  input  in_16,
  input  in_17,
  output out_18,
  output out_19,
  output out_20,
  output out_21,
  output out_22,
  output out_23,
  output out_24,
  output out_25,
  output out_26
);

  wire clock_1_out, contador8bits_1_out_11;

  somador_clocked somador_clocked_1 (
    .Y(in_2), .in_10(in_3), .in_11(in_4), .in_12(in_5), .in_13(in_6), .in_14(in_7), .in_15(in_8),
    .in_16(in_9), .Z(out_18), .out_19(out_19), .out_20(out_20), .out_21(out_21), .out_22(out_22),
    .out_23(out_23), .out_24(out_24), .out_25(out_25), .out_26(out_26), .in_1(out_19), .in_2(out_20),
    .in_3(out_21), .in_4(out_22), .in_5(out_23), .in_6(out_24), .in_8(out_25), .in_7(out_18),
    .Clock(contador8bits_1_out_11));
  Clock clock_1 (.out(clock_1_out));
  contador8bits contador8bits_1 (
    .Clear(in_1), .out_11(contador8bits_1_out_11), .Clock(clock_1_out), .in_1(in_10), .in_2(in_11),
    .in_3(in_12), .in_4(in_13), .in_5(in_14), .in_6(in_15), .in_7(in_16), .in_8(in_17));

  // Other names for the same wires on the sheet: _1 = in_2; _2 = in_3; _3 = in_4; _4 = in_5; _5 = in_6; _6 = in_7;
  //   _7 = in_8; _8 = in_9; A = out_18; B = out_19; C = out_20; D = out_21; E = out_22; F = out_23; G = out_24;
  //   H = out_25; O = out_26
endmodule

module somador_clocked (
  input  in_1,
  input  in_2,
  input  in_3,
  input  in_4,
  input  in_5,
  input  in_6,
  input  in_7,
  input  in_8,
  input  Y,
  input  in_10,
  input  in_11,
  input  in_12,
  input  in_13,
  input  in_14,
  input  in_15,
  input  in_16,
  input  Clock,
  output Z,
  output out_19,
  output out_20,
  output out_21,
  output out_22,
  output out_23,
  output out_24,
  output out_25,
  output out_26
);

  wire and_1_out, and_2_out, and_3_out, and_4_out, and_5_out, and_6_out, and_7_out, and_8_out, and_9_out,
       and_10_out, and_11_out, and_12_out, and_13_out, and_14_out, and_15_out, d_ff_1_q, d_ff_2_q, d_ff_3_q,
       d_ff_4_q, d_ff_5_q, d_ff_6_q, d_ff_7_q, d_ff_8_q, or_1_out, or_2_out, or_3_out, or_4_out, or_5_out,
       or_6_out, xor_2_out, xor_4_out, xor_6_out, xor_8_out, xor_10_out, xor_12_out, xor_14_out;

  D_Flip_Flop d_ff_1 (.clk(Clock), .D(in_7), .Q(d_ff_1_q));  // open: Qn, preset, en, reset
  xor xor_1 (Z, d_ff_1_q, Y);
  and and_1 (and_1_out, Y, d_ff_1_q);
  D_Flip_Flop d_ff_2 (.D(in_1), .Q(d_ff_2_q));  // open: clk, Qn, preset, en, reset
  xor xor_2 (xor_2_out, d_ff_2_q, in_10);
  xor xor_3 (out_19, xor_2_out, and_1_out);
  and and_2 (and_2_out, in_10, d_ff_2_q);
  and and_3 (and_3_out, and_1_out, xor_2_out);
  or or_1 (or_1_out, and_2_out, and_3_out);
  D_Flip_Flop d_ff_3 (.clk(Clock), .D(in_2), .Q(d_ff_3_q));  // open: Qn, preset, en, reset
  xor xor_4 (xor_4_out, d_ff_3_q, in_11);
  xor xor_5 (out_20, xor_4_out, or_1_out);
  and and_4 (and_4_out, in_11, d_ff_3_q);
  and and_5 (and_5_out, or_1_out, xor_4_out);
  or or_2 (or_2_out, and_4_out, and_5_out);
  D_Flip_Flop d_ff_4 (.clk(Clock), .D(in_3), .Q(d_ff_4_q));  // open: Qn, preset, en, reset
  xor xor_6 (xor_6_out, d_ff_4_q, in_12);
  xor xor_7 (out_21, xor_6_out, or_2_out);
  and and_6 (and_6_out, in_12, d_ff_4_q);
  and and_7 (and_7_out, or_2_out, xor_6_out);
  or or_3 (or_3_out, and_6_out, and_7_out);
  D_Flip_Flop d_ff_5 (.clk(Clock), .D(in_4), .Q(d_ff_5_q));  // open: Qn, preset, en, reset
  xor xor_8 (xor_8_out, d_ff_5_q, in_13);
  xor xor_9 (out_22, xor_8_out, or_3_out);
  and and_8 (and_8_out, in_13, d_ff_5_q);
  and and_9 (and_9_out, or_3_out, xor_8_out);
  or or_4 (or_4_out, and_8_out, and_9_out);
  D_Flip_Flop d_ff_6 (.clk(Clock), .D(in_5), .Q(d_ff_6_q));  // open: Qn, preset, en, reset
  xor xor_10 (xor_10_out, d_ff_6_q, in_14);
  xor xor_11 (out_23, xor_10_out, or_4_out);
  and and_10 (and_10_out, in_14, d_ff_6_q);
  or or_5 (or_5_out, and_10_out, and_11_out);
  D_Flip_Flop d_ff_7 (.clk(Clock), .D(in_6), .Q(d_ff_7_q));  // open: Qn, preset, en, reset
  and and_11 (and_11_out, or_4_out, xor_10_out);
  xor xor_12 (xor_12_out, d_ff_7_q, in_15);
  xor xor_13 (out_24, xor_12_out, or_5_out);
  and and_12 (and_12_out, in_15, d_ff_7_q);
  and and_13 (and_13_out, or_5_out, xor_12_out);
  or or_6 (or_6_out, and_12_out, and_13_out);
  D_Flip_Flop d_ff_8 (.clk(Clock), .D(in_8), .Q(d_ff_8_q));  // open: Qn, preset, en, reset
  xor xor_14 (xor_14_out, d_ff_8_q, in_16);
  xor xor_15 (out_25, xor_14_out, or_6_out);
  and and_14 (and_14_out, in_16, d_ff_8_q);
  and and_15 (and_15_out, or_6_out, xor_14_out);
  or or_7 (out_26, and_14_out, and_15_out);

  // Notes on the sheet:
  //   in_16: pull=down
  //   in_15: pull=down
  //   in_10: pull=down
  //   in_13: pull=down
  //   Y: pull=down
  //   in_14: pull=down
  //   in_12: pull=down
  //   in_11: pull=down
  //   carry out
  //   carry out
  //   carry out
  //   carry out
  //   carry out
  //   carry out
  //   carry out
  //   overflow
  //   carry out
endmodule

module contador8bits (
  input  in_1,
  input  in_2,
  input  in_3,
  input  in_4,
  input  in_5,
  input  in_6,
  input  in_7,
  input  in_8,
  input  Clock,
  input  Clear,
  output out_11
);

  wire j_k_ff_1_q, j_k_ff_2_q, j_k_ff_3_q, j_k_ff_4_q, j_k_ff_5_q, j_k_ff_6_q, j_k_ff_7_q, j_k_ff_8_q,
       or_1_out, xor_1_out, xor_2_out, xor_3_out, xor_4_out, xor_5_out, xor_6_out, xor_7_out, xor_8_out;

  xor xor_1 (xor_1_out, in_1, j_k_ff_1_q);
  J_K_Flip_Flop #(.trigger("falling")) j_k_ff_1 (
    .J(1'b1), .clk(out_11), .K(1'b1), .Q(j_k_ff_1_q), .reset(Clear));  // open: Qn, preset, en
  and and_1 (out_11, Clock, or_1_out);
  xor xor_2 (xor_2_out, in_2, j_k_ff_2_q);
  J_K_Flip_Flop #(.trigger("falling")) j_k_ff_2 (
    .J(1'b1), .clk(j_k_ff_1_q), .K(1'b1), .Q(j_k_ff_2_q), .reset(Clear));  // open: Qn, preset, en
  xor xor_3 (xor_3_out, in_3, j_k_ff_3_q);
  J_K_Flip_Flop #(.trigger("falling")) j_k_ff_3 (
    .J(1'b1), .clk(j_k_ff_2_q), .K(1'b1), .Q(j_k_ff_3_q), .reset(Clear));  // open: Qn, preset, en
  or or_1 (or_1_out, xor_1_out, xor_2_out, xor_3_out, xor_4_out, xor_5_out, xor_6_out, xor_8_out, xor_7_out);
  xor xor_4 (xor_4_out, in_4, j_k_ff_4_q);
  J_K_Flip_Flop #(.trigger("falling")) j_k_ff_4 (
    .J(1'b1), .clk(j_k_ff_3_q), .K(1'b1), .Q(j_k_ff_4_q), .reset(Clear));  // open: Qn, preset, en
  xor xor_5 (xor_5_out, in_5, j_k_ff_5_q);
  J_K_Flip_Flop #(.trigger("falling")) j_k_ff_5 (
    .J(1'b1), .clk(j_k_ff_4_q), .K(1'b1), .Q(j_k_ff_5_q), .reset(Clear));  // open: Qn, preset, en
  xor xor_6 (xor_6_out, in_6, j_k_ff_6_q);
  J_K_Flip_Flop #(.trigger("falling")) j_k_ff_6 (
    .J(1'b1), .clk(j_k_ff_5_q), .K(1'b1), .Q(j_k_ff_6_q), .reset(Clear));  // open: Qn, preset, en
  xor xor_7 (xor_7_out, in_8, j_k_ff_7_q);
  xor xor_8 (xor_8_out, in_7, j_k_ff_8_q);
  J_K_Flip_Flop #(.trigger("falling")) j_k_ff_7 (
    .J(1'b1), .clk(j_k_ff_8_q), .K(1'b1), .Q(j_k_ff_7_q), .reset(Clear));  // open: Qn, preset, en
  J_K_Flip_Flop #(.trigger("falling")) j_k_ff_8 (
    .J(1'b1), .clk(j_k_ff_6_q), .K(1'b1), .Q(j_k_ff_8_q), .reset(Clear));  // open: Qn, preset, en
endmodule
