// Logisim project subtrac.circ as structural Verilog: 1 circuit, main circuit main
module main (
  input  Carry_In,
  input  A0,
  input  B0,
  input  A1,
  input  B1,
  input  A2,
  input  B2,
  input  A3,
  input  B3,
  input  A4,
  input  B4,
  input  A5,
  input  B5,
  input  A6,
  input  B6,
  input  A7,
  input  B7,
  output S0,
  output S1,
  output S2,
  output S3,
  output S4,
  output S5,
  output S6,
  output S7,
  output Carry_Out,
  output Overlow
);

  wire and_1_out, and_2_out, and_3_out, and_4_out, and_5_out, and_6_out, and_7_out, and_8_out, and_9_out,
       and_10_out, and_11_out, and_12_out, and_13_out, and_14_out, and_15_out, and_16_out, and_17_out,
       and_18_out, and_19_out, and_20_out, and_21_out, and_22_out, and_23_out, and_24_out, and_25_out,
       and_26_out, not_1_out, not_2_out, not_3_out, or_1_out, or_2_out, or_3_out, or_4_out, or_5_out,
       or_6_out, or_7_out, xor_1_out, xor_2_out, xor_3_out, xor_4_out, xor_5_out, xor_6_out, xor_7_out,
       xor_8_out, xor_9_out, xor_10_out, xor_11_out, xor_12_out, xor_13_out, xor_14_out, xor_15_out,
       xor_16_out;

  xor xor_1 (xor_1_out, Carry_In, B0);
  xor xor_2 (xor_2_out, Carry_In, B1);
  xor xor_3 (xor_3_out, Carry_In, B2);
  xor xor_4 (xor_4_out, Carry_In, B3);
  xor xor_5 (xor_5_out, Carry_In, B4);
  xor xor_6 (xor_6_out, Carry_In, B5);
  xor xor_7 (xor_7_out, Carry_In, B6);
  xor xor_8 (xor_8_out, Carry_In, B7);
  xor xor_9 (xor_9_out, A0, xor_1_out);
  and and_1 (and_1_out, A0, A0, xor_1_out);
  and and_2 (and_2_out, A0, Carry_In);
  and and_3 (and_3_out, xor_1_out, Carry_In);
  xor xor_10 (xor_10_out, A1, xor_2_out);
  and and_4 (and_4_out, A1, xor_2_out);
  and and_5 (and_5_out, A1, or_1_out);
  and and_6 (and_6_out, xor_2_out, or_1_out);
  xor xor_11 (xor_11_out, A2, xor_3_out);
  and and_7 (and_7_out, A2, xor_3_out);
  and and_8 (and_8_out, A2, or_2_out);
  and and_9 (and_9_out, xor_3_out, or_2_out);
  xor xor_12 (xor_12_out, A3, xor_4_out);
  and and_10 (and_10_out, A3, xor_4_out);
  and and_11 (and_11_out, A3, or_3_out);
  and and_12 (and_12_out, xor_4_out, or_3_out);
  xor xor_13 (xor_13_out, A4, xor_5_out);
  and and_13 (and_13_out, A4, xor_5_out);
  and and_14 (and_14_out, A4, or_4_out);
  and and_15 (and_15_out, xor_5_out, or_4_out);
  xor xor_14 (xor_14_out, A5, xor_6_out);
  and and_16 (and_16_out, A5, A5);
  and and_17 (and_17_out, A5, or_5_out);
  buf and_18 (and_18_out, or_5_out);  // AND_Gate
  xor xor_15 (xor_15_out, A6, xor_7_out);
  and and_19 (and_19_out, A6, xor_7_out);
  and and_20 (and_20_out, A6, or_6_out);
  and and_21 (and_21_out, xor_7_out, or_6_out);
  xor xor_16 (xor_16_out, A7, xor_8_out);
  and and_22 (and_22_out, A7, A7);
  and and_23 (and_23_out, A7, or_7_out);
  and and_24 (and_24_out, A7, or_7_out);
  not not_1 (not_1_out, A7);
  not not_2 (not_2_out, A7);
  xor xor_17 (S0, Carry_In, xor_9_out);
  or or_1 (or_1_out, and_1_out, and_2_out, and_3_out);
  xor xor_18 (S1, or_1_out, xor_10_out);
  or or_2 (or_2_out, and_4_out, and_5_out, and_6_out);
  xor xor_19 (S2, or_2_out, xor_11_out);
  or or_3 (or_3_out, and_7_out, and_8_out, and_9_out);
  xor xor_20 (S3, or_3_out, xor_12_out);
  or or_4 (or_4_out, and_10_out, and_11_out, and_12_out);
  xor xor_21 (S4, or_4_out, xor_13_out);
  or or_5 (or_5_out, and_13_out, and_14_out, and_15_out);
  xor xor_22 (S5, or_5_out, xor_14_out);
  or or_6 (or_6_out, and_16_out, and_16_out, and_17_out, and_18_out);
  xor xor_23 (S6, or_6_out, xor_15_out);
  or or_7 (or_7_out, and_19_out, and_20_out, and_21_out);
  xor xor_24 (S7, or_7_out, xor_16_out);
  or or_8 (Carry_Out, and_22_out, and_23_out, and_24_out);
  not not_3 (not_3_out, S7);
  and and_25 (and_25_out, not_1_out, not_1_out, not_2_out, S7);
  and and_26 (and_26_out, A7, A7, not_3_out);
  or or_9 (Overlow, and_25_out, and_26_out);
endmodule
